// Logisim project 1.1三输入多数表决器.circ as structural Verilog: 1 circuit, main circuit main
module main (
  input  A,
  input  B,
  input  C,
  output F
);

  wire and_1_out, and_2_out, and_3_out;

  and and_1 (and_1_out, A, C);
  and and_2 (and_2_out, A, B);
  and and_3 (and_3_out, B, C);
  or or_1 (F, and_1_out, and_2_out, and_3_out);
endmodule
