// Logisim project 2-1MUX-1.circ as structural Verilog: 1 circuit, main circuit main
module main (
  input  D0,
  input  D1,
  input  S,
  output Y
);

  wire and_1_out, and_2_out, not_1_out;

  // Probe on S
  not not_1 (not_1_out, S);
  // Probe on not_1_out
  and and_1 (and_1_out, D0, not_1_out);
  and and_2 (and_2_out, D1, S);
  or or_1 (Y, and_1_out, and_2_out);
endmodule
