// Logisim project 思考题5.circ as structural Verilog: 1 circuit, main circuit main
// 奇偶检验
module main (
  input  in_1,
  input  in_2,
  input  in_3,
  input  in_4,
  output out_5
);

  wire and_1_out, and_2_out, and_3_out, and_4_out, and_5_out, and_6_out, and_7_out, and_8_out;

  and and_1 (and_1_out, ~in_1, ~in_2, ~in_3, in_4);  // AND_Gate
  and and_2 (and_2_out, ~in_1, ~in_2, in_3, ~in_4);  // AND_Gate
  and and_3 (and_3_out, ~in_1, in_2, ~in_3, ~in_4);  // AND_Gate
  and and_4 (and_4_out, in_1, ~in_2, ~in_3, ~in_4);  // AND_Gate
  and and_5 (and_5_out, ~in_1, in_2, in_3, in_4);  // AND_Gate
  and and_6 (and_6_out, in_1, ~in_2, in_3, in_4);  // AND_Gate
  and and_7 (and_7_out, in_1, in_2, ~in_3, in_4);  // AND_Gate
  and and_8 (and_8_out, in_1, in_2, in_3, ~in_4);  // AND_Gate
  or or_1 (out_5, and_1_out, and_2_out, and_3_out, and_4_out, and_5_out, and_6_out, and_7_out, and_8_out);
endmodule
