// Logisim project 2-3 FA.circ as structural Verilog: 2 circuits, main circuit 4FA
module FA (
  input  A,
  input  B,
  input  CI,
  output S,
  output CO
);

  wire and_1_out, and_2_out, xor_1_out;

  and and_1 (and_1_out, B, A);
  xor xor_1 (xor_1_out, A, B);
  and and_2 (and_2_out, xor_1_out, CI);
  xor xor_2 (S, xor_1_out, CI);
  or or_1 (CO, and_2_out, and_1_out);
endmodule

module _4FA (
  input  CI,
  input  [3:0] A,
  input  [3:0] B,
  output [3:0] S,
  output CO
);

  wire fa_1_co, fa_2_co, fa_3_co;

  FA fa_1 (.A(A[0]), .B(B[0]), .CI(CI), .S(S[0]), .CO(fa_1_co));
  FA fa_2 (.A(A[1]), .B(B[1]), .CI(fa_1_co), .S(S[1]), .CO(fa_2_co));
  FA fa_3 (.A(A[2]), .B(B[2]), .CI(fa_2_co), .S(S[2]), .CO(fa_3_co));
  FA fa_4 (.A(A[3]), .B(B[3]), .CI(fa_3_co), .S(S[3]), .CO(CO));
endmodule
