// Logisim project 2-4 ALU.circ as structural Verilog: 2 circuits, main circuit main
module main (
  input  A,
  input  B,
  input  [2:0] in_3,
  output F
);

  wire adder_1_out, and_1_out, not_1_out, not_2_out, or_1_out, subtractor_1_out, xnor_1_out;

  Adder #(.width(1)) adder_1 (.a(A), .b(B), .out(adder_1_out));  // open: cin, cout
  Subtractor #(.width(1)) subtractor_1 (.a(A), .b(B), .out(subtractor_1_out));  // open: bin, bout
  and and_1 (and_1_out, A, B);
  or or_1 (or_1_out, A, B);
  xnor xnor_1 (xnor_1_out, A, B);
  not not_1 (not_1_out, A);
  not not_2 (not_2_out, B);
  Multiplexer #(.select(3), .enable("false")) multiplexer_1 (
    .in0(adder_1_out), .in1(subtractor_1_out), .in2(and_1_out), .in3(or_1_out), .in4(xnor_1_out),
    .in5(not_1_out), .in6(A), .in7(not_2_out), .out(F), .sel(in_3));
endmodule

module _4ALU (
  input  [3:0] A,
  input  [3:0] B,
  input  [2:0] in_3,
  output [3:0] F
);

  wire [3:0] adder_1_out, and_1_out, not_1_out, not_2_out, or_1_out, subtractor_1_out, xnor_1_out;

  Adder #(.width(4)) adder_1 (.a(A), .b(B), .out(adder_1_out));  // open: cin, cout
  Subtractor #(.width(4)) subtractor_1 (.a(A), .b(B), .out(subtractor_1_out));  // open: bin, bout
  assign and_1_out = A & B;  // AND_Gate and_1, 4 bits wide
  assign or_1_out = A | B;  // OR_Gate or_1, 4 bits wide
  assign xnor_1_out = ~(A ^ B);  // XNOR_Gate xnor_1, 4 bits wide
  assign not_1_out = ~A;  // NOT_Gate not_1, 4 bits wide
  assign not_2_out = ~B;  // NOT_Gate not_2, 4 bits wide
  Multiplexer #(.select(3), .width(4), .enable("false")) multiplexer_1 (
    .in0(adder_1_out), .in1(subtractor_1_out), .in2(and_1_out), .in3(or_1_out), .in4(xnor_1_out),
    .in5(not_1_out), .in6(A), .in7(not_2_out), .out(F), .sel(in_3));
endmodule
