// Logisim project 2-5 Ham.circ as structural Verilog: 3 circuits, main circuit main
module main (
  input  [6:0] in_1,
  input  G2B_L,
  input  G2A_L,
  input  G1,
  output out_5,
  output [6:0] out_6
);

  wire \n3_8译码器_1_y0_l , \n3_8译码器_1_y1_l , \n3_8译码器_1_y2_l , \n3_8译码器_1_y3_l , \n3_8译码器_1_y4_l ,
       \n3_8译码器_1_y5_l , \n3_8译码器_1_y6_l , \n3_8译码器_1_y7_l , \n4位偶校验器_1_out_5 , \n4位偶校验器_2_out_5 ,
       \n4位偶校验器_3_out_5 , not_2_out, not_3_out, not_4_out, not_5_out, not_6_out, not_7_out, not_8_out;

  \_4位偶校验器  \u_4位偶校验器_1  (.in_1(in_1[6]), .in_2(in_1[4]), .in_3(in_1[2]), .in_4(in_1[0]), .out_5(\n4位偶校验器_1_out_5 ));
  \_4位偶校验器  \u_4位偶校验器_2  (.in_1(in_1[6]), .in_2(in_1[5]), .in_3(in_1[2]), .in_4(in_1[1]), .out_5(\n4位偶校验器_2_out_5 ));
  \_4位偶校验器  \u_4位偶校验器_3  (.in_1(in_1[6]), .in_2(in_1[5]), .in_3(in_1[4]), .in_4(in_1[3]), .out_5(\n4位偶校验器_3_out_5 ));
  \_3_8译码器  \u_3_8译码器_1  (
    .G1(G1), .G2A_L(G2A_L), .G2B_L(G2B_L), .A(\n4位偶校验器_1_out_5 ), .B(\n4位偶校验器_2_out_5 ),
    .C(\n4位偶校验器_3_out_5 ), .Y0_L(\n3_8译码器_1_y0_l ), .Y1_L(\n3_8译码器_1_y1_l ), .Y2_L(\n3_8译码器_1_y2_l ),
    .Y3_L(\n3_8译码器_1_y3_l ), .Y4_L(\n3_8译码器_1_y4_l ), .Y5_L(\n3_8译码器_1_y5_l ), .Y6_L(\n3_8译码器_1_y6_l ),
    .Y7_L(\n3_8译码器_1_y7_l ));
  not not_1 (out_5, \n3_8译码器_1_y0_l );
  xor xor_1 (out_6[0], in_1[0], not_2_out);
  not not_2 (not_2_out, \n3_8译码器_1_y1_l );
  xor xor_2 (out_6[1], in_1[1], not_3_out);
  not not_3 (not_3_out, \n3_8译码器_1_y2_l );
  xor xor_3 (out_6[2], in_1[2], not_4_out);
  not not_4 (not_4_out, \n3_8译码器_1_y3_l );
  xor xor_4 (out_6[3], in_1[3], not_5_out);
  not not_5 (not_5_out, \n3_8译码器_1_y4_l );
  xor xor_5 (out_6[4], in_1[4], not_6_out);
  not not_6 (not_6_out, \n3_8译码器_1_y5_l );
  xor xor_6 (out_6[5], in_1[5], not_7_out);
  not not_7 (not_7_out, \n3_8译码器_1_y6_l );
  xor xor_7 (out_6[6], in_1[6], not_8_out);
  not not_8 (not_8_out, \n3_8译码器_1_y7_l );
endmodule

module \_4位偶校验器  (
  input  in_1,
  input  in_2,
  input  in_3,
  input  in_4,
  output out_5
);

  wire xor_1_out, xor_2_out;

  xor xor_1 (xor_1_out, in_1, in_2);
  xor xor_2 (xor_2_out, in_3, in_4);
  xor xor_3 (out_5, xor_1_out, xor_2_out);
endmodule

module \_3_8译码器  (
  input  G1,
  input  G2A_L,
  input  G2B_L,
  input  A,
  input  B,
  input  C,
  output Y0_L,
  output Y1_L,
  output Y2_L,
  output Y3_L,
  output Y4_L,
  output Y5_L,
  output Y6_L,
  output Y7_L
);

  wire and_1_out, and_2_out, and_3_out, and_4_out, and_5_out, and_6_out, and_7_out, and_8_out, and_9_out,
       not_1_out, not_2_out, not_3_out, not_4_out, not_5_out, not_6_out, not_7_out;

  not not_1 (not_1_out, G1);
  and and_1 (and_1_out, ~not_1_out, ~G2A_L, ~G2B_L);  // AND_Gate
  not not_2 (not_2_out, A);
  not not_3 (not_3_out, B);
  not not_4 (not_4_out, C);
  not not_5 (not_5_out, not_2_out);
  not not_6 (not_6_out, not_3_out);
  not not_7 (not_7_out, not_4_out);
  not not_8 (Y0_L, and_2_out);
  and and_2 (and_2_out, not_2_out, not_3_out, not_4_out, and_1_out);
  not not_9 (Y1_L, and_3_out);
  and and_3 (and_3_out, not_5_out, not_3_out, not_4_out, and_1_out);
  not not_10 (Y2_L, and_4_out);
  and and_4 (and_4_out, not_2_out, not_4_out, not_6_out, and_1_out);
  not not_11 (Y3_L, and_5_out);
  and and_5 (and_5_out, not_4_out, not_5_out, not_6_out, and_1_out);
  not not_12 (Y4_L, and_6_out);
  and and_6 (and_6_out, not_2_out, not_3_out, not_7_out, and_1_out);
  and and_7 (and_7_out, not_3_out, not_5_out, not_7_out, and_1_out);
  not not_13 (Y5_L, and_7_out);
  and and_8 (and_8_out, not_2_out, not_6_out, not_7_out, and_1_out);
  not not_14 (Y6_L, and_8_out);
  and and_9 (and_9_out, not_5_out, not_6_out, not_7_out, and_1_out);
  not not_15 (Y7_L, and_9_out);
endmodule
