// Logisim project NJUCS.circ as structural Verilog: 1 circuit, main circuit main
module main (
  input  [6:0] in_1,
  input  [6:0] in_2,
  input  [6:0] in_3,
  input  [6:0] in_4,
  input  [6:0] in_5,
  input  [6:0] in_6,
  input  [6:0] in_7,
  input  [6:0] in_8,
  input  [6:0] in_9,
  input  [6:0] in_10,
  input  [6:0] in_11,
  input  [6:0] in_12,
  input  [6:0] in_13,
  input  [6:0] in_14,
  input  [6:0] in_15,
  input  [6:0] in_16,
  input  [6:0] in_17,
  input  [6:0] in_18,
  input  [6:0] in_19,
  input  [6:0] in_20,
  input  [6:0] in_21,
  input  [6:0] in_22,
  input  [6:0] in_23,
  input  [6:0] in_24,
  input  [6:0] in_25,
  input  [6:0] in_26,
  input  [6:0] in_27,
  input  [6:0] in_28,
  input  [6:0] in_29,
  input  [6:0] in_30,
  input  [6:0] in_31
);

  DotMatrix #(.matrixcols(30)) dotmatrix_1 (
    .col0(in_2), .col1(in_4), .col2(in_6), .col3(in_8), .col4(in_10), .col5(in_12), .col6(in_14),
    .col7(in_16), .col8(in_18), .col9(in_20), .col10(in_22), .col11(in_24), .col12(in_26), .col13(in_28),
    .col14(in_29), .col15(in_30), .col16(in_31), .col17(in_1), .col18(in_3), .col19(in_5), .col20(in_7),
    .col21(in_9), .col22(in_11), .col23(in_13), .col24(in_15), .col25(in_17), .col26(in_19), .col27(in_21),
    .col28(in_23), .col29(in_25));
endmodule
