// Logisim project 思考题5.circ as structural Verilog: 1 circuit, main circuit main
module main (
  input  [3:0] A,
  input  [3:0] B,
  input  [2:0] in_3,
  output OF,
  output CF,
  output CF_2,
  output ZF,
  output SF,
  output [3:0] F
);

  wire or_2_out, subtractor_1_bout, xor_2_out, xor_3_out;
  wire [3:0] adder_1_out, and_1_out, not_1_out, not_2_out, or_1_out, subtractor_1_out, xor_1_out;

  Adder #(.width(4)) adder_1 (.a(A), .b(B), .out(adder_1_out), .cout(CF));  // open: cin
  Subtractor #(.width(4)) subtractor_1 (.a(A), .b(B), .out(subtractor_1_out), .bout(subtractor_1_bout));  // open: bin
  assign and_1_out = A & B;  // AND_Gate and_1, 4 bits wide
  assign or_1_out = A | B;  // OR_Gate or_1, 4 bits wide
  assign xor_1_out = A ^ B;  // XOR_Gate xor_1, 4 bits wide
  assign not_1_out = ~A;  // NOT_Gate not_1, 4 bits wide
  assign not_2_out = ~B;  // NOT_Gate not_2, 4 bits wide
  not not_3 (CF_2, subtractor_1_bout);
  Multiplexer #(.select(3), .width(4), .enable("false")) multiplexer_1 (
    .in0(adder_1_out), .in1(subtractor_1_out), .in2(and_1_out), .in3(or_1_out), .in4(xor_1_out),
    .in5(not_1_out), .in6(A), .in7(not_2_out), .out(F), .sel(in_3));
  xor xor_2 (xor_2_out, B[3], A[3]);
  or or_2 (or_2_out, F[0], F[1], F[2], F[3]);
  xor xor_3 (xor_3_out, xor_2_out, F[3]);
  not not_4 (ZF, or_2_out);
  xor xor_4 (OF, CF, xor_3_out);

  assign SF = F[3];
endmodule
