// Logisim project 思考题2-60进制计数器.circ as structural Verilog: 2 circuits, main circuit main
module main (
  input  LD,
  input  EN
);

  wire and_1_out, and_2_out, and_3_out, cntr4u_1_rco, cntr4u_2_rco;
  wire [3:0] cntr4u_1_q0, cntr4u_2_q0;

  Clock CLK ();  // open: out
  CNTR4U cntr4u_1 (
    .LD(LD), .CLR(and_1_out), .D0(1'b0), .D1(1'b0), .D2(1'b0), .D3(1'b0), .ENP(EN), .ENT(EN),
    .Q0(cntr4u_1_q0[0]), .Q1(cntr4u_1_q0[1]), .Q2(cntr4u_1_q0[2]), .Q3(cntr4u_1_q0[3]), .RCO(cntr4u_1_rco));
  and and_1 (and_1_out, cntr4u_1_q0[0], ~cntr4u_1_q0[1], ~cntr4u_1_q0[2], cntr4u_1_q0[3]);  // AND_Gate
  CNTR4U cntr4u_2 (
    .LD(LD), .CLR(and_2_out), .D0(1'b0), .D1(1'b0), .D2(1'b0), .D3(1'b0), .ENP(and_3_out), .ENT(and_3_out),
    .Q0(cntr4u_2_q0[0]), .Q1(cntr4u_2_q0[1]), .Q2(cntr4u_2_q0[2]), .Q3(cntr4u_2_q0[3]), .RCO(cntr4u_2_rco));
  and and_2 (and_2_out, ~cntr4u_2_q0[0], cntr4u_2_q0[1], cntr4u_2_q0[2]);  // AND_Gate
  and and_3 (and_3_out, ~cntr4u_1_q0[0], ~cntr4u_1_q0[1], ~cntr4u_1_q0[2], ~cntr4u_1_q0[3]);  // AND_Gate
  LED led_1 (.in(cntr4u_1_rco));
  LED led_2 (.in(cntr4u_2_rco));
  Hex_Digit_Display hex_digit_display_1 (.value(cntr4u_2_q0));  // open: dp
  Hex_Digit_Display hex_digit_display_2 (.value(cntr4u_1_q0));  // open: dp
endmodule

module CNTR4U (
  input  LD,
  input  CLR,
  input  D0,
  input  D1,
  input  D2,
  input  D3,
  input  ENP,
  input  ENT,
  output Q0,
  output Q1,
  output Q2,
  output Q3,
  output RCO
);

  wire and_1_out, and_2_out, and_3_out, and_4_out, and_5_out, and_6_out, and_7_out, and_8_out, and_10_out,
       and_11_out, and_12_out, and_13_out, and_14_out, and_15_out, and_16_out, and_17_out, buffer_1_out,
       CLK_out, d_ff_1_qn, d_ff_2_qn, d_ff_3_qn, d_ff_4_qn, not_1_out, not_2_out, not_3_out, or_1_out,
       or_2_out, or_3_out, or_4_out, xor_1_out, xor_2_out, xor_3_out, xor_4_out;

  Clock CLK (.out(CLK_out));
  buf buffer_1 (buffer_1_out, CLR);
  not not_1 (not_1_out, CLK_out);
  not not_2 (not_2_out, d_ff_1_qn);
  and and_1 (and_1_out, ~d_ff_2_qn, ~d_ff_1_qn);  // AND_Gate
  and and_2 (and_2_out, ~d_ff_3_qn, ~d_ff_2_qn, ~d_ff_1_qn);  // AND_Gate
  and and_3 (and_3_out, ENP, ENT);
  and and_4 (and_4_out, LD, ~buffer_1_out);  // AND_Gate
  and and_5 (and_5_out, not_2_out, and_3_out);
  and and_6 (and_6_out, and_1_out, and_3_out);
  and and_7 (and_7_out, and_2_out, and_3_out);
  not not_3 (not_3_out, ENT);
  and and_8 (and_8_out, ~and_4_out, ~buffer_1_out);  // AND_Gate
  xor xor_1 (xor_1_out, and_3_out, ~d_ff_1_qn);  // XOR_Gate
  xor xor_2 (xor_2_out, and_5_out, ~d_ff_2_qn);  // XOR_Gate
  xor xor_3 (xor_3_out, and_6_out, ~d_ff_3_qn);  // XOR_Gate
  xor xor_4 (xor_4_out, and_7_out, ~d_ff_4_qn);  // XOR_Gate
  and and_9 (RCO, ~d_ff_4_qn, ~d_ff_3_qn, ~d_ff_2_qn, ~d_ff_1_qn, ~not_3_out);  // AND_Gate
  and and_10 (and_10_out, and_4_out, D0);
  and and_11 (and_11_out, and_8_out, xor_1_out);
  and and_12 (and_12_out, and_4_out, D1);
  and and_13 (and_13_out, and_8_out, xor_2_out);
  and and_14 (and_14_out, and_4_out, D2);
  and and_15 (and_15_out, and_8_out, xor_3_out);
  and and_16 (and_16_out, and_4_out, D3);
  and and_17 (and_17_out, and_8_out, xor_4_out);
  or or_1 (or_1_out, and_10_out, and_11_out);
  or or_2 (or_2_out, and_12_out, and_13_out);
  or or_3 (or_3_out, and_14_out, and_15_out);
  or or_4 (or_4_out, and_16_out, and_17_out);
  D_Flip_Flop #(.trigger("falling")) d_ff_1 (
    .clk(not_1_out), .D(or_1_out), .Q(Q0), .Qn(d_ff_1_qn), .preset(1'b0), .reset(1'b0));
  D_Flip_Flop #(.trigger("falling")) d_ff_2 (
    .clk(not_1_out), .D(or_2_out), .Q(Q1), .Qn(d_ff_2_qn), .preset(1'b0), .reset(1'b0));
  D_Flip_Flop #(.trigger("falling")) d_ff_3 (
    .clk(not_1_out), .D(or_3_out), .Q(Q2), .Qn(d_ff_3_qn), .preset(1'b0), .reset(1'b0));
  D_Flip_Flop #(.trigger("falling")) d_ff_4 (
    .clk(not_1_out), .D(or_4_out), .Q(Q3), .Qn(d_ff_4_qn), .preset(1'b0), .reset(1'b0));
endmodule
