// Logisim project 思考题4.circ as structural Verilog: 1 circuit, main circuit main
module main (
  input  [1:0] \移动位数 ,
  input  \符号判断 ,
  input  \移动方向 ,
  input  D3,
  input  D2,
  input  D1,
  input  D0,
  input  CLR,
  output Q3,
  output Q2,
  output Q1,
  output Q0
);

  wire and_1_out, and_2_out, and_3_out, and_4_out, and_5_out, and_6_out, CLK_out, decoder_1_out0,
       decoder_1_out1, decoder_1_out2, decoder_1_out3, or_1_out, or_2_out, or_3_out, or_4_out, \初始_2_out ,
       \初始_3_out , \初始_4_out , \初始_out , \右移1_2_out , \右移1_3_out , \右移1_4_out , \右移1_out , \右移2_2_out ,
       \右移2_3_out , \右移2_4_out , \右移2_out , \右移3_2_out , \右移3_3_out , \右移3_4_out , \右移3_out , \左移0_2_out ,
       \左移0_3_out , \左移0_4_out , \左移0_out , \左移1_2_out , \左移1_3_out , \左移1_4_out , \左移1_out , \左移2_2_out ,
       \左移2_3_out , \左移2_4_out , \左移2_out , \左移3_2_out , \左移3_3_out , \左移3_4_out , \左移3_out ;

  and and_1 (and_1_out, \符号判断 , Q3);
  and and_2 (and_2_out, ~\符号判断 , Q3);  // AND_Gate
  Decoder #(.select(2), .enable("false")) decoder_1 (
    .out0(decoder_1_out0), .out1(decoder_1_out1), .out2(decoder_1_out2), .out3(decoder_1_out3), .sel(\移动位数 ));
  and \u_初始  (\初始_out , decoder_1_out0, D3, \移动方向 );
  and \u_右移1  (\右移1_out , decoder_1_out1, and_1_out, \移动方向 );
  and \u_右移2  (\右移2_out , decoder_1_out2, and_1_out, \移动方向 );
  and \u_右移3  (\右移3_out , decoder_1_out3, and_1_out, \移动方向 );
  and \u_左移0  (\左移0_out , decoder_1_out0, Q3, ~\移动方向 );  // AND_Gate
  and \u_左移1  (\左移1_out , decoder_1_out1, Q2, ~\移动方向 );  // AND_Gate
  and \u_左移2  (\左移2_out , decoder_1_out2, Q1, ~\移动方向 );  // AND_Gate
  and \u_左移3  (\左移3_out , decoder_1_out3, Q0, ~\移动方向 );  // AND_Gate
  and \u_初始_2  (\初始_2_out , decoder_1_out0, D2, \移动方向 );
  and \u_右移1_2  (\右移1_2_out , decoder_1_out1, and_2_out, \移动方向 );
  and \u_右移2_2  (\右移2_2_out , decoder_1_out2, 1'b0, \移动方向 );
  and \u_右移3_2  (\右移3_2_out , decoder_1_out3, 1'b0, \移动方向 );
  and \u_左移0_2  (\左移0_2_out , decoder_1_out0, Q2, ~\移动方向 );  // AND_Gate
  and \u_左移1_2  (\左移1_2_out , decoder_1_out1, Q1, ~\移动方向 );  // AND_Gate
  and \u_左移2_2  (\左移2_2_out , decoder_1_out2, Q0, ~\移动方向 );  // AND_Gate
  and \u_左移3_2  (\左移3_2_out , decoder_1_out3, 1'b0, ~\移动方向 );  // AND_Gate
  and \u_初始_3  (\初始_3_out , decoder_1_out0, D1, \移动方向 );
  and \u_右移1_3  (\右移1_3_out , decoder_1_out1, Q2, \移动方向 );
  and \u_右移2_3  (\右移2_3_out , decoder_1_out2, and_2_out, \移动方向 );
  and \u_右移3_3  (\右移3_3_out , decoder_1_out3, 1'b0, \移动方向 );
  and \u_左移0_3  (\左移0_3_out , decoder_1_out0, Q1, ~\移动方向 );  // AND_Gate
  and \u_左移1_3  (\左移1_3_out , decoder_1_out1, Q0, ~\移动方向 );  // AND_Gate
  and \u_左移2_3  (\左移2_3_out , decoder_1_out2, 1'b0, ~\移动方向 );  // AND_Gate
  and \u_左移3_3  (\左移3_3_out , decoder_1_out3, 1'b0, ~\移动方向 );  // AND_Gate
  and \u_初始_4  (\初始_4_out , decoder_1_out0, D0, \移动方向 );
  and \u_右移1_4  (\右移1_4_out , decoder_1_out1, Q1, \移动方向 );
  and \u_右移2_4  (\右移2_4_out , decoder_1_out2, Q2, \移动方向 );
  and \u_右移3_4  (\右移3_4_out , decoder_1_out3, and_2_out, \移动方向 );
  and \u_左移0_4  (\左移0_4_out , decoder_1_out0, Q0, ~\移动方向 );  // AND_Gate
  and \u_左移1_4  (\左移1_4_out , decoder_1_out1, 1'b0, ~\移动方向 );  // AND_Gate
  and \u_左移2_4  (\左移2_4_out , decoder_1_out2, 1'b0, ~\移动方向 );  // AND_Gate
  and \u_左移3_4  (\左移3_4_out , decoder_1_out3, 1'b0, ~\移动方向 );  // AND_Gate
  or or_1 (or_1_out, \初始_out , \右移1_out , \右移2_out , \右移3_out , \左移0_out , \左移1_out , \左移2_out , \左移3_out );
  or or_2 (or_2_out, \初始_2_out , \右移1_2_out , \右移2_2_out , \右移3_2_out , \左移0_2_out , \左移1_2_out , \左移2_2_out , \左移3_2_out );
  or or_3 (or_3_out, \初始_3_out , \右移1_3_out , \右移2_3_out , \右移3_3_out , \左移0_3_out , \左移1_3_out , \左移2_3_out , \左移3_3_out );
  or or_4 (or_4_out, \初始_4_out , \右移1_4_out , \右移2_4_out , \右移3_4_out , \左移0_4_out , \左移1_4_out , \左移2_4_out , \左移3_4_out );
  and and_3 (and_3_out, or_1_out, ~CLR);  // AND_Gate
  and and_4 (and_4_out, or_2_out, ~CLR);  // AND_Gate
  and and_5 (and_5_out, or_3_out, ~CLR);  // AND_Gate
  and and_6 (and_6_out, or_4_out, ~CLR);  // AND_Gate
  Clock CLK (.out(CLK_out));
  D_Flip_Flop d_ff_1 (.clk(CLK_out), .D(and_3_out), .Q(Q3));  // open: Qn, preset, reset
  D_Flip_Flop d_ff_2 (.clk(CLK_out), .D(and_4_out), .Q(Q2));  // open: Qn, preset, reset
  D_Flip_Flop d_ff_3 (.clk(CLK_out), .D(and_5_out), .Q(Q1));  // open: Qn, preset, reset
  D_Flip_Flop d_ff_4 (.clk(CLK_out), .D(and_6_out), .Q(Q0));  // open: Qn, preset, reset
endmodule
