// Logisim project oj4.circ as structural Verilog: 9 circuits, main circuit main
module main (
  output _passed,
  output A,
  output B,
  output [3:0] C,
  output D,
  output E,
  output halt,
  output F,
  output G,
  output H,
  output I,
  output J,
  output K,
  output L,
  output M,
  output N,
  output O,
  output [15:0] P,
  output Q,
  output X,
  output S,
  output T,
  output [31:0] R,
  output U,
  output [31:0] V,
  output W
);

  wire clk0, clk1, clk2, clk3, clk4, clk5, clock_1_out, counter_1_carry, counter_2_carry, counter_3_carry,
       counter_4_carry, counter_5_carry, counter_6_carry, counter_7_carry, counter_8_carry, counter_9_carry,
       counter_10_q, counter_11_q, counter_12_q, counter_13_q, halt0, halt1, halt2, halt3, halt4;
  wire [2:0] counter_14_q;
  wire [3:0] counter_1_q, counter_2_q, counter_6_q, counter_7_q, multiplexer_1_out;
  wire [7:0] counter_3_q, counter_4_q, counter_8_q, counter_9_q;
  wire [12:0] counter_5_q;
  wire [31:0] ram_1_data;

  Counter #(.width(4), .max('hf)) counter_1 (
    .count(1'b1), .Q(counter_1_q), .carry(counter_1_carry), .clk(clk0));  // open: load, D, clr, preset, down
  Counter #(.width(4), .max('hf)) counter_2 (
    .count(1'b1), .Q(counter_2_q), .carry(counter_2_carry), .clk(clk1));  // open: load, D, clr, preset, down
  Counter counter_3 (
    .count(1'b1), .Q(counter_3_q), .carry(counter_3_carry), .clk(clk2));  // open: load, D, clr, preset, down
  Counter counter_4 (
    .count(1'b1), .Q(counter_4_q), .carry(counter_4_carry), .clk(clk3));  // open: load, D, clr, preset, down
  Counter #(.width(13), .max('h1fff)) counter_5 (
    .count(1'b1), .Q(counter_5_q), .carry(counter_5_carry), .clk(clk4));  // open: load, D, clr, preset, down
  Counter #(.width(4), .max('hf)) counter_6 (
    .count(1'b1), .Q(counter_6_q), .carry(counter_6_carry), .clk(counter_1_carry));  // open: load, D, clr, preset, down
  Counter #(.width(4), .max('hf)) counter_7 (
    .count(1'b1), .Q(counter_7_q), .carry(counter_7_carry), .clk(counter_2_carry));  // open: load, D, clr, preset, down
  Counter counter_8 (
    .count(1'b1), .Q(counter_8_q), .carry(counter_8_carry), .clk(counter_3_carry));  // open: load, D, clr, preset, down
  Counter counter_9 (
    .count(1'b1), .Q(counter_9_q), .carry(counter_9_carry), .clk(counter_4_carry));  // open: load, D, clr, preset, down
  Counter #(.width(1), .max('h1)) counter_10 (
    .count(1'b1), .Q(counter_10_q), .carry(halt0), .clk(counter_6_carry));  // open: load, D, clr, preset, down
  CLA4 cla4_1 (.A(counter_6_q), .B(counter_1_q), .C0(counter_10_q), .C4(A), .Gg(B), .S(C), .Pg(D), .C3(E));
  Counter #(.width(1), .max('h1)) counter_11 (
    .count(1'b1), .Q(counter_11_q), .carry(halt1), .clk(counter_7_carry));  // open: load, D, clr, preset, down
  RAM #(.addrWidth(13), .dataWidth(32), .Select("low")) ram_1 (
    .addr(counter_5_q), .data(ram_1_data), .ld(1'b1));  // open: sel, clk, clr
  CLU4 clu4_1 (
    .G3(counter_7_q[0]), .P3(counter_2_q[0]), .G2(counter_7_q[1]), .P2(counter_2_q[1]), .G1(counter_7_q[2]),
    .P1(counter_2_q[2]), .G0(counter_7_q[3]), .P0(counter_2_q[3]), .C0(counter_11_q), .Gs0(F), .C4(G),
    .C3(H), .C2(I), .C1(J), .Ps0(K));
  Counter #(.width(1), .max('h1)) counter_12 (
    .count(1'b1), .Q(counter_12_q), .carry(halt2), .clk(counter_8_carry));  // open: load, D, clr, preset, down
  Counter #(.width(1), .max('h1)) counter_13 (
    .count(1'b1), .Q(counter_13_q), .carry(halt3), .clk(counter_9_carry));  // open: load, D, clr, preset, down
  Counter #(.width(3), .max('h7)) counter_14 (
    .count(1'b1), .Q(counter_14_q), .clk(counter_5_carry));  // open: load, D, carry, clr, preset, down
  CLA16 cla16_1 (
    .A({counter_8_q[5], counter_3_q[6], counter_3_q[4], counter_3_q[2], counter_8_q[4], counter_3_q[5], counter_8_q[6], counter_3_q[1], counter_8_q[0], counter_3_q[7], counter_3_q[0], counter_8_q[3], counter_3_q[3], counter_8_q[7], counter_8_q[1], counter_8_q[2]}),
    .B({counter_8_q[6], counter_8_q[2], counter_3_q[4], counter_3_q[5], counter_3_q[3], counter_8_q[4], counter_3_q[7], counter_8_q[5], counter_8_q[7], counter_3_q[6], counter_3_q[2], counter_8_q[1:0], counter_3_q[0], counter_8_q[3], counter_3_q[1]}),
    .C0(counter_12_q), .C16(L), .C15(M), .Gs0(N), .Ps0(O), .S(P));
  Multiplexer #(.select(3), .width(4), .enable("false")) multiplexer_1 (
    .in0(4'b0000), .in1(4'b0010), .in2(4'b0011), .in3(4'b0110), .in4(4'b1000), .in5(4'b1111), .in6(4'b0000),
    .in7(4'b0000), .out(multiplexer_1_out), .sel(counter_14_q));
  Adder32 adder32_1 (
    .A({counter_4_q[3], counter_9_q[3], counter_4_q[4], counter_9_q[7:6], counter_4_q[0], counter_4_q[7], counter_4_q[2], counter_9_q[4], counter_9_q[0], counter_4_q[4], counter_9_q[1], counter_4_q[6:5], counter_4_q[3], counter_9_q[3], counter_4_q[6], counter_9_q[4], counter_4_q[1], counter_4_q[5], counter_9_q[0], counter_9_q[1], counter_4_q[0], counter_9_q[2], counter_9_q[5], counter_9_q[2], counter_4_q[7], counter_9_q[5], counter_4_q[2], counter_9_q[6], counter_9_q[7], counter_4_q[1]}),
    .B({counter_4_q[2], counter_9_q[7], counter_4_q[1], counter_4_q[5], counter_9_q[7], counter_4_q[5], counter_4_q[3], counter_4_q[6], counter_4_q[0], {2{counter_4_q[4]}}, counter_9_q[5], counter_9_q[3:2], counter_4_q[2], counter_9_q[1], counter_4_q[0], counter_9_q[1], counter_4_q[1], counter_9_q[0], counter_9_q[4], counter_4_q[3], counter_9_q[4], counter_9_q[5], counter_9_q[6], counter_4_q[6], counter_9_q[3], counter_4_q[7], counter_9_q[2], counter_9_q[6], counter_9_q[0], counter_4_q[7]}),
    .C(counter_13_q), .ZF(X), .F(R), .OF(S), .COUT(U), .CF(Q), .SF(T));
  ALU alu_1 (
    .A({ram_1_data[14], ram_1_data[10], ram_1_data[20], ram_1_data[25], ram_1_data[21], ram_1_data[1], ram_1_data[18], ram_1_data[5], ram_1_data[27], ram_1_data[28], ram_1_data[23], ram_1_data[24], ram_1_data[4], ram_1_data[0], ram_1_data[26], ram_1_data[22], ram_1_data[19], ram_1_data[13], ram_1_data[2], ram_1_data[3], ram_1_data[11], ram_1_data[31], ram_1_data[15], ram_1_data[12], ram_1_data[9], ram_1_data[29], ram_1_data[17], ram_1_data[30], ram_1_data[7:6], ram_1_data[8], ram_1_data[16]}),
    .B({ram_1_data[14], ram_1_data[10], ram_1_data[20], ram_1_data[25], ram_1_data[21], ram_1_data[1], ram_1_data[18], ram_1_data[5], ram_1_data[27], ram_1_data[28], ram_1_data[23], ram_1_data[24], ram_1_data[4], ram_1_data[0], ram_1_data[26], ram_1_data[22], ram_1_data[19], ram_1_data[13], ram_1_data[2], ram_1_data[3], ram_1_data[11], ram_1_data[31], ram_1_data[15], ram_1_data[12], ram_1_data[9], ram_1_data[29], ram_1_data[17], ram_1_data[30], ram_1_data[7:6], ram_1_data[8], ram_1_data[16]}),
    .ALUctr(multiplexer_1_out), .Results(V), .zero(W));
  Clock clock_1 (.out(clock_1_out));
  Demultiplexer #(.select(3), .enable("false")) demultiplexer_1 (
    .out0(clk0), .out1(clk1), .out2(clk2), .out3(clk3), .out4(clk4), .out5(clk5), .in(clock_1_out),
    .sel(3'b100));  // open: out6, out7
  Comparator #(.width(3), .mode("unsigned")) comparator_1 (.a(counter_14_q), .b(3'b101), .gt(halt4));  // open: eq, lt
  or or_1 (halt, halt0, halt1, halt2, halt3, halt4);

  assign _passed = 1'b1;

  // Notes on the sheet:
  //   请勿修改此电路中除解复用器选择段常数外的任何内容!
  //   请勿修改此电路中除解复用器选择段常数外的任何内容!
  //   请勿修改此电路中除解复用器选择段常数外的任何内容!
  //   请勿修改此电路中除解复用器选择段常数外的任何内容!
  //   0 - 4位CLA测试电路
  //   1 - 4位CLU测试电路
  //   请勿修改此电路中除解复用器选择段常数外的任何内容!
  //   ↑依据所测试的电路修改该常量
  //   0 - 4位CLA测试电路
  //   1 - 4位CLU测试电路
  //   2 - 16位CLU测试电路
  //   3 - Adder32测试电路
  //   4 - ALU测试电路
  //   2 - 16位CLU测试电路
  //   3 - Adder32测试电路
  //   4 - ALU测试电路
endmodule

module CLA4 (
  input  [3:0] A,
  input  [3:0] B,
  input  C0,
  output C4,
  output Gg,
  output [3:0] S,
  output Pg,
  output C3
);

  wire and_1_out, and_2_out, and_3_out, and_5_out, and_6_out, and_7_out, and_8_out, and_9_out, and_10_out,
       and_11_out, and_12_out, and_13_out, and_14_out, and_15_out, and_16_out, and_17_out, and_18_out,
       and_21_out, and_22_out, nand_1_out, nand_2_out, nand_3_out, nand_4_out, nor_1_out, nor_2_out,
       nor_3_out, nor_4_out, not_1_out, not_2_out, not_3_out, not_4_out, not_5_out, not_6_out, not_7_out,
       not_8_out, not_9_out, not_10_out, not_11_out, not_12_out, not_13_out, not_14_out, not_15_out,
       not_16_out, not_17_out;

  not not_1 (not_1_out, C0);
  nand nand_1 (nand_1_out, B[3], A[3]);
  nor nor_1 (nor_1_out, B[3], A[3]);
  nand nand_2 (nand_2_out, B[2], A[2]);
  nor nor_2 (nor_2_out, B[2], A[2]);
  nand nand_3 (nand_3_out, B[1], A[1]);
  nor nor_3 (nor_3_out, B[1], A[1]);
  nand nand_4 (nand_4_out, B[0], A[0]);
  nor nor_4 (nor_4_out, B[0], A[0]);
  not not_2 (not_2_out, nand_1_out);
  and and_1 (and_1_out, ~nor_1_out, ~nand_2_out);  // AND_Gate
  and and_2 (and_2_out, ~nor_1_out, ~nand_3_out, ~nor_2_out);  // AND_Gate
  and and_3 (and_3_out, ~nor_1_out, ~nor_2_out, ~nor_3_out, ~nand_4_out);  // AND_Gate
  and and_4 (Pg, ~nor_1_out, ~nor_2_out, ~nor_3_out, ~nor_4_out);  // AND_Gate
  or or_1 (Gg, not_2_out, and_1_out, and_2_out, and_3_out);
  not not_3 (not_3_out, nor_1_out);
  not not_4 (not_4_out, and_5_out);
  and and_5 (and_5_out, nor_2_out, nand_1_out);
  not not_5 (not_5_out, and_6_out);
  and and_6 (and_6_out, nor_3_out, nand_1_out, nand_2_out);
  and and_7 (and_7_out, nor_4_out, nand_1_out, nand_2_out, nand_3_out);
  not not_6 (not_6_out, and_7_out);
  and and_8 (and_8_out, nand_1_out, nand_2_out, nand_3_out, nand_4_out, not_1_out);
  not not_7 (not_7_out, and_8_out);
  and and_9 (and_9_out, nand_1_out, ~nor_1_out);  // AND_Gate
  not not_8 (not_8_out, nor_2_out);
  not not_9 (not_9_out, and_10_out);
  and and_10 (and_10_out, nor_3_out, nand_2_out);
  not not_10 (not_10_out, and_11_out);
  and and_11 (and_11_out, nor_4_out, nand_3_out, nand_2_out);
  and and_12 (and_12_out, not_1_out, nand_2_out, nand_3_out, nand_4_out);
  not not_11 (not_11_out, and_12_out);
  and and_13 (and_13_out, nand_2_out, ~nor_2_out);  // AND_Gate
  not not_12 (not_12_out, nor_3_out);
  not not_13 (not_13_out, and_14_out);
  and and_14 (and_14_out, nor_4_out, nand_3_out);
  not not_14 (not_14_out, and_15_out);
  and and_15 (and_15_out, nand_4_out, nand_3_out, not_1_out);
  and and_16 (and_16_out, nand_3_out, ~nor_3_out);  // AND_Gate
  not not_15 (not_15_out, nor_4_out);
  and and_17 (and_17_out, nand_4_out, not_1_out);
  not not_16 (not_16_out, and_17_out);
  and and_18 (and_18_out, nand_4_out, ~nor_4_out);  // AND_Gate
  not not_17 (not_17_out, not_1_out);
  and and_19 (C4, not_3_out, not_4_out, not_5_out, not_6_out, not_7_out);
  and and_20 (C3, not_8_out, not_9_out, not_10_out, not_11_out);
  and and_21 (and_21_out, not_12_out, not_13_out, not_14_out);
  and and_22 (and_22_out, not_15_out, not_16_out);
  xor xor_1 (S[3], and_9_out, C3);
  xor xor_2 (S[2], and_13_out, and_21_out);
  xor xor_3 (S[1], and_16_out, and_22_out);
  xor xor_4 (S[0], and_18_out, not_17_out);

  // Notes on the sheet:
  //   请勿修改各引脚相对位置!
  //   在这里实现你的电路
  //   在这里实现你的电路
endmodule

module CLU4 (
  input  G3,
  input  P3,
  input  G2,
  input  P2,
  input  G1,
  input  P1,
  input  G0,
  input  P0,
  input  C0,
  output Gs0,
  output C4,
  output C3,
  output C2,
  output C1,
  output Ps0
);

  wire and_1_out, and_2_out, and_3_out, C1_t, nor_1_out, nor_2_out, nor_3_out, nor_4_out, nor_5_out,
       nor_6_out, nor_7_out, nor_8_out, nor_9_out, nor_10_out, not_1_out, not_2_out, not_3_out, not_4_out,
       not_5_out, not_6_out, not_7_out, not_8_out, not_9_out, not_10_out, not_11_out, not_12_out, not_13_out;

  not not_1 (not_1_out, G3);
  not not_2 (not_2_out, P3);
  not not_3 (not_3_out, G2);
  not not_4 (not_4_out, P2);
  not not_5 (not_5_out, G1);
  not not_6 (not_6_out, P1);
  not not_7 (not_7_out, G0);
  not not_8 (not_8_out, P0);
  not not_9 (not_9_out, C0);
  not not_10 (not_10_out, not_1_out);
  nor nor_1 (nor_1_out, not_2_out, not_3_out);
  nor nor_2 (nor_2_out, not_2_out, not_4_out, not_5_out);
  nor nor_3 (nor_3_out, not_2_out, not_4_out, not_6_out, not_7_out);
  nor nor_4 (nor_4_out, not_2_out, not_4_out, not_6_out, not_8_out, not_9_out);
  not not_11 (not_11_out, not_3_out);
  nor nor_5 (nor_5_out, not_4_out, not_5_out);
  nor nor_6 (nor_6_out, not_4_out, not_6_out, not_7_out);
  nor nor_7 (nor_7_out, not_4_out, not_6_out, not_8_out, not_9_out);
  not not_12 (not_12_out, not_5_out);
  nor nor_8 (nor_8_out, not_6_out, not_7_out);
  nor nor_9 (nor_9_out, not_6_out, not_8_out, not_9_out);
  not not_13 (not_13_out, not_7_out);
  nor nor_10 (nor_10_out, not_8_out, not_9_out);
  or or_1 (C4, not_10_out, nor_1_out, nor_2_out, nor_3_out, nor_4_out);
  or or_2 (C3, not_11_out, nor_5_out, nor_6_out, nor_7_out);
  or or_3 (C1, not_12_out, nor_8_out, nor_9_out);
  or or_4 (C1_t, not_13_out, nor_10_out);
  and and_1 (and_1_out, P3, G2);
  and and_2 (and_2_out, P3, P2, G1);
  and and_3 (and_3_out, P3, P2, P1, G0);
  and and_4 (Ps0, P3, P2, P0, P1);
  or or_5 (Gs0, G3, and_1_out, and_2_out, and_3_out);

  assign C2 = C1;

  // Notes on the sheet:
  //   请勿修改各引脚相对位置!
  //   在这里实现你的电路
  //   在这里实现你的电路
endmodule

module CLA16 (
  input  [15:0] A,
  input  [15:0] B,
  input  C0,
  output C16,
  output C15,
  output Gs0,
  output Ps0,
  output [15:0] S
);

  wire \修改后cla_1_gg , \修改后cla_1_pg , \修改后cla_2_gg , \修改后cla_2_pg , \修改后cla_3_gg , \修改后cla_3_pg ,
       \修改后cla_4_gg , \修改后cla_4_pg , \修改后clu_1_c1 , \修改后clu_1_c2 , \修改后clu_1_c3 ;

  \修改后CLA  \u_修改后cla_1  (
    .A(A[15:12]), .B(B[15:12]), .C0(\修改后clu_1_c3 ), .Gg(\修改后cla_1_gg ), .C4(C16), .C3(C15), .S(S[15:12]),
    .Pg(\修改后cla_1_pg ));
  \修改后CLA  \u_修改后cla_2  (
    .A(A[11:8]), .B(B[11:8]), .C0(\修改后clu_1_c2 ), .Gg(\修改后cla_2_gg ), .S(S[11:8]), .Pg(\修改后cla_2_pg ));  // open: C4, C3
  \修改后CLA  \u_修改后cla_3  (
    .A(A[7:4]), .B(B[7:4]), .C0(\修改后clu_1_c1 ), .Gg(\修改后cla_3_gg ), .S(S[7:4]), .Pg(\修改后cla_3_pg ));  // open: C4, C3
  \修改后CLA  \u_修改后cla_4  (
    .A(A[3:0]), .B(B[3:0]), .C0(C0), .Gg(\修改后cla_4_gg ), .S(S[3:0]), .Pg(\修改后cla_4_pg ));  // open: C4, C3
  \修改后CLU  \u_修改后clu_1  (
    .G3(\修改后cla_1_gg ), .P3(\修改后cla_1_pg ), .G2(\修改后cla_2_gg ), .P2(\修改后cla_2_pg ), .G1(\修改后cla_3_gg ),
    .P1(\修改后cla_3_pg ), .G0(\修改后cla_4_gg ), .P0(\修改后cla_4_pg ), .C0(C0), .Gs0(Gs0), .Ps0(Ps0),
    .C3(\修改后clu_1_c3 ), .C2(\修改后clu_1_c2 ), .C1(\修改后clu_1_c1 ));

  // Notes on the sheet:
  //   请勿修改各引脚相对位置!
endmodule

module Adder32 (
  input  [31:0] A,
  input  [31:0] B,
  input  C,
  output ZF,
  output [31:0] F,
  output OF,
  output COUT,
  output CF,
  output SF
);

  wire cla16_1_c16, cla16_2_c15;

  CLA16 cla16_1 (.A(A[15:0]), .B(B[15:0]), .C0(C), .C16(cla16_1_c16), .S(F[15:0]));  // open: C15, Gs0, Ps0
  CLA16 cla16_2 (
    .A(A[31:16]), .B(B[31:16]), .C0(cla16_1_c16), .C16(COUT), .C15(cla16_2_c15), .S(F[31:16]));  // open: Gs0, Ps0
  xor xor_1 (OF, COUT, cla16_2_c15);
  xor xor_2 (CF, COUT, C);
  nor nor_1 (ZF, F[16], F[17], F[18], F[19], F[20], F[21], F[22], F[23], F[24], F[25], F[26], F[27], F[28], F[29], F[30], F[31], F[0], F[1], F[2], F[3], F[4], F[5], F[6], F[7], F[8], F[9], F[10], F[11], F[12], F[13], F[14], F[15]);

  assign SF = F[31];

  // Notes on the sheet:
  //   请勿修改各引脚相对位置!
endmodule

module \ALU控制信号转换  (
  input  [3:0] ALUctr,
  output [1:0] OPctr,
  output SiGctr,
  output SUBctr
);

  wire and_1_out, and_2_out, and_3_out, and_4_out, and_5_out;

  and and_1 (and_1_out, ~ALUctr[0], ~ALUctr[3], ALUctr[1], ALUctr[2]);  // AND_Gate
  and and_2 (and_2_out, ALUctr[1], ~ALUctr[2], ~ALUctr[3]);  // AND_Gate
  and and_3 (and_3_out, ALUctr[0], ALUctr[1], ALUctr[2], ALUctr[3]);
  and and_4 (and_4_out, ALUctr[1], ~ALUctr[2], ~ALUctr[3]);  // AND_Gate
  and and_5 (and_5_out, ALUctr[1], ~ALUctr[2], ~ALUctr[3]);  // AND_Gate
  or or_1 (OPctr[0], and_1_out, and_2_out);
  not not_1 (SiGctr, ALUctr[0]);
  or or_2 (OPctr[1], and_3_out, and_4_out);
  or or_3 (SUBctr, and_5_out, ALUctr[3]);

  // Notes on the sheet:
  //   请勿修改各引脚相对位置!
endmodule

module ALU (
  input  [31:0] A,
  input  [31:0] B,
  input  [3:0] ALUctr,
  output [31:0] Results,
  output zero
);

  wire adder32_1_cf, adder32_1_of, adder32_1_sf, \alu控制信号转换_1_sigctr , \alu控制信号转换_1_subctr ,
       multiplexer_1_out, xor_2_out;
  wire [1:0] \alu控制信号转换_1_opctr ;
  wire [31:0] adder32_1_f, bit_extender_1_out, bit_extender_2_out, or_1_out, xor_1_out;

  assign bit_extender_1_out = {{31{\alu控制信号转换_1_subctr }}, \alu控制信号转换_1_subctr };  // Bit_Extender bit_extender_1
  assign xor_1_out = B ^ bit_extender_1_out;  // XOR_Gate xor_1, 32 bits wide
  assign or_1_out = A | B;  // OR_Gate or_1, 32 bits wide
  Adder32 adder32_1 (
    .A(A), .B(xor_1_out), .C(\alu控制信号转换_1_subctr ), .ZF(zero), .F(adder32_1_f), .OF(adder32_1_of),
    .CF(adder32_1_cf), .SF(adder32_1_sf));  // open: COUT
  \ALU控制信号转换  \alu控制信号转换_1  (
    .ALUctr(ALUctr), .OPctr(\alu控制信号转换_1_opctr ), .SiGctr(\alu控制信号转换_1_sigctr ), .SUBctr(\alu控制信号转换_1_subctr ));
  xor xor_2 (xor_2_out, adder32_1_of, adder32_1_sf);
  Multiplexer #(.enable("false")) multiplexer_1 (
    .in0(adder32_1_cf), .in1(xor_2_out), .out(multiplexer_1_out), .sel(\alu控制信号转换_1_sigctr ));
  Multiplexer #(.select(2), .width(32), .enable("false")) multiplexer_2 (
    .in0(adder32_1_f), .in1(or_1_out), .in2(B), .in3(bit_extender_2_out), .out(Results),
    .sel(\alu控制信号转换_1_opctr ));
  assign bit_extender_2_out = {{31{1'b0}}, multiplexer_1_out};  // Bit_Extender bit_extender_2

  // Notes on the sheet:
  //   请勿修改各引脚相对位置!
endmodule

module \修改后CLA  (
  input  [3:0] A,
  input  [3:0] B,
  input  C0,
  output Gg,
  output C4,
  output C3,
  output [3:0] S,
  output Pg
);

  wire and_1_out, and_2_out, and_3_out, and_5_out, and_6_out, and_7_out, and_8_out, and_10_out, and_11_out,
       nand_1_out, nand_2_out, nand_3_out, nand_4_out, nor_1_out, nor_2_out, nor_3_out, nor_4_out, not_1_out,
       not_2_out, not_3_out, not_4_out, not_5_out, not_6_out, not_7_out, or_2_out, or_3_out, or_4_out,
       or_5_out, or_6_out, or_7_out, or_8_out, or_9_out, or_10_out, or_11_out;

  not not_1 (not_1_out, C0);
  nand nand_1 (nand_1_out, B[3], A[3]);
  nor nor_1 (nor_1_out, B[3], A[3]);
  nand nand_2 (nand_2_out, B[2], A[2]);
  nor nor_2 (nor_2_out, B[2], A[2]);
  nand nand_3 (nand_3_out, B[1], A[1]);
  nor nor_3 (nor_3_out, B[1], A[1]);
  nand nand_4 (nand_4_out, B[0], A[0]);
  nor nor_4 (nor_4_out, B[0], A[0]);
  not not_2 (not_2_out, nand_1_out);
  and and_1 (and_1_out, ~nor_1_out, ~nand_2_out);  // AND_Gate
  and and_2 (and_2_out, ~nor_1_out, ~nor_2_out, ~nand_3_out);  // AND_Gate
  and and_3 (and_3_out, ~nor_1_out, ~nor_2_out, ~nor_3_out, ~nand_4_out);  // AND_Gate
  and and_4 (Pg, ~nor_1_out, ~nor_2_out, ~nor_3_out, ~nor_4_out);  // AND_Gate
  or or_1 (Gg, not_2_out, and_1_out, and_2_out, and_3_out);
  not not_3 (not_3_out, nor_1_out);
  or or_2 (or_2_out, ~nand_1_out, ~nor_2_out);  // OR_Gate
  or or_3 (or_3_out, ~nand_1_out, ~nand_2_out, ~nor_3_out);  // OR_Gate
  or or_4 (or_4_out, ~nand_1_out, ~nand_2_out, ~nand_3_out, ~nor_4_out);  // OR_Gate
  or or_5 (or_5_out, ~nand_1_out, ~nand_2_out, ~nand_3_out, ~nand_4_out, ~not_1_out);  // OR_Gate
  and and_5 (and_5_out, nand_1_out, ~nor_1_out);  // AND_Gate
  not not_4 (not_4_out, nor_2_out);
  or or_6 (or_6_out, ~nand_2_out, ~nor_3_out);  // OR_Gate
  or or_7 (or_7_out, ~nand_2_out, ~nand_3_out, ~nor_4_out);  // OR_Gate
  or or_8 (or_8_out, ~nand_2_out, ~nand_3_out, ~nand_4_out, ~not_1_out);  // OR_Gate
  and and_6 (and_6_out, nand_2_out, ~nor_2_out);  // AND_Gate
  not not_5 (not_5_out, nor_3_out);
  or or_9 (or_9_out, ~nand_3_out, ~nor_4_out);  // OR_Gate
  or or_10 (or_10_out, ~nand_3_out, ~nand_4_out, ~not_1_out);  // OR_Gate
  and and_7 (and_7_out, nand_3_out, ~nor_3_out);  // AND_Gate
  not not_6 (not_6_out, nor_4_out);
  or or_11 (or_11_out, ~not_1_out, ~nand_4_out);  // OR_Gate
  and and_8 (and_8_out, nand_4_out, ~nor_4_out);  // AND_Gate
  not not_7 (not_7_out, not_1_out);
  and and_9 (C3, not_4_out, or_6_out, or_7_out, or_8_out);
  and and_10 (and_10_out, or_9_out, or_10_out, not_5_out);
  and and_11 (and_11_out, not_6_out, or_11_out);
  and and_12 (C4, not_3_out, or_2_out, or_3_out, or_4_out, or_5_out);
  xor xor_1 (S[3], and_5_out, C3);
  xor xor_2 (S[2], and_6_out, and_10_out);
  xor xor_3 (S[1], and_7_out, and_11_out);
  xor xor_4 (S[0], and_8_out, not_7_out);
endmodule

module \修改后CLU  (
  input  G3,
  input  P3,
  input  G2,
  input  P2,
  input  G1,
  input  P1,
  input  G0,
  input  P0,
  input  C0,
  output Gs0,
  output Ps0,
  output C3,
  output C2,
  output C1
);

  wire and_1_out, and_2_out, and_3_out, and_5_out, and_6_out, and_7_out, and_8_out, and_9_out, and_10_out;

  and and_1 (and_1_out, P3, G2);
  and and_2 (and_2_out, P3, P2, G1);
  and and_3 (and_3_out, P3, P2, P1, G0);
  and and_4 (Ps0, P3, P2, P0, P1);
  and and_5 (and_5_out, P2, G1);
  and and_6 (and_6_out, P2, P1, G0);
  and and_7 (and_7_out, P2, P1, P0, C0);
  and and_8 (and_8_out, P1, G0);
  and and_9 (and_9_out, C0, P0, P1);
  and and_10 (and_10_out, P0, C0);
  or or_1 (Gs0, G3, and_1_out, and_2_out, and_3_out);
  or or_2 (C3, G2, and_5_out, and_6_out, and_7_out);
  or or_3 (C2, and_9_out, and_8_out, G1);
  or or_4 (C1, and_10_out, G0);
endmodule
