// Logisim project lab5.circ as structural Verilog
module \ASCII码显示实验  (
  input  [7:0] ASCII_CODE,
  input  Sel,
  output [7:0] out_3,
  output [7:0] out_4,
  output [7:0] out_5,
  output [7:0] out_6,
  output [7:0] out_7,
  output [7:0] out_8,
  output [7:0] out_9,
  output [7:0] out_10,
  output [7:0] out_11,
  output [7:0] out_12,
  output [7:0] out_13,
  output [7:0] out_14,
  output [7:0] out_15,
  output [7:0] out_16,
  output [7:0] out_17,
  output [7:0] out_18
);

  wire [15:0] adder_1_out, adder_2_out, adder_3_out, adder_4_out, adder_5_out, adder_6_out, adder_7_out,
       adder_8_out, adder_9_out, adder_10_out, adder_11_out, adder_12_out, adder_13_out, adder_14_out,
       adder_15_out, adder_16_out, bit_extender_1_out;

  assign bit_extender_1_out = {{8{1'b0}}, ASCII_CODE};  // Bit_Extender bit_extender_1
  Shifter #(.width(16)) shifter_1 (.\dist (4'b0100));  // open: in, out
  Adder #(.width(16)) adder_1 (.a(bit_extender_1_out), .b({16{1'b0}}), .out(adder_1_out));  // open: cin, cout
  Adder #(.width(16)) adder_2 (.a(bit_extender_1_out), .b(16'h2), .out(adder_2_out));  // open: cin, cout
  Adder #(.width(16)) adder_3 (.a(bit_extender_1_out), .b(16'h4), .out(adder_3_out));  // open: cin, cout
  Adder #(.width(16)) adder_4 (.a(bit_extender_1_out), .b(16'h6), .out(adder_4_out));  // open: cin, cout
  Adder #(.width(16)) adder_5 (.a(bit_extender_1_out), .b(16'h8), .out(adder_5_out));  // open: cin, cout
  Adder #(.width(16)) adder_6 (.a(bit_extender_1_out), .b(16'ha), .out(adder_6_out));  // open: cin, cout
  Adder #(.width(16)) adder_7 (.a(bit_extender_1_out), .b(16'hc), .out(adder_7_out));  // open: cin, cout
  Adder #(.width(16)) adder_8 (.a(bit_extender_1_out), .b(16'he), .out(adder_8_out));  // open: cin, cout
  ROM #(.addrWidth(16), .Select("high")) rom_1 (.addr(adder_1_out), .data(out_3), .sel(Sel));
  ROM #(.addrWidth(16), .Select("high")) rom_2 (.addr(adder_2_out), .data(out_5), .sel(Sel));
  ROM #(.addrWidth(16), .Select("high")) rom_3 (.addr(adder_3_out), .data(out_7), .sel(Sel));
  ROM #(.addrWidth(16), .Select("high")) rom_4 (.addr(adder_4_out), .data(out_9), .sel(Sel));
  ROM #(.addrWidth(16), .Select("high")) rom_5 (.addr(adder_5_out), .data(out_11), .sel(Sel));
  ROM #(.addrWidth(16), .Select("high")) rom_6 (.addr(adder_6_out), .data(out_13), .sel(Sel));
  ROM #(.addrWidth(16), .Select("high")) rom_7 (.addr(adder_7_out), .data(out_15), .sel(Sel));
  ROM #(.addrWidth(16), .Select("high")) rom_8 (.addr(adder_8_out), .data(out_17), .sel(Sel));
  DotMatrix #(.inputtype("row"), .matrixcols(8), .matrixrows(16)) dotmatrix_1 (
    .row0(out_3), .row1(out_4), .row2(out_5), .row3(out_6), .row4(out_7), .row5(out_8), .row6(out_9),
    .row7(out_10), .row8(out_11), .row9(out_12), .row10(out_13), .row11(out_14), .row12(out_15),
    .row13(out_16), .row14(out_17), .row15(out_18));
  Adder #(.width(16)) adder_9 (.a(bit_extender_1_out), .b(16'h1), .out(adder_9_out));  // open: cin, cout
  Adder #(.width(16)) adder_10 (.a(bit_extender_1_out), .b(16'h3), .out(adder_10_out));  // open: cin, cout
  Adder #(.width(16)) adder_11 (.a(bit_extender_1_out), .b(16'h5), .out(adder_11_out));  // open: cin, cout
  Adder #(.width(16)) adder_12 (.a(bit_extender_1_out), .b(16'h7), .out(adder_12_out));  // open: cin, cout
  Adder #(.width(16)) adder_13 (.a(bit_extender_1_out), .b(16'h9), .out(adder_13_out));  // open: cin, cout
  Adder #(.width(16)) adder_14 (.a(bit_extender_1_out), .b(16'hb), .out(adder_14_out));  // open: cin, cout
  Adder #(.width(16)) adder_15 (.a(bit_extender_1_out), .b(16'hd), .out(adder_15_out));  // open: cin, cout
  Adder #(.width(16)) adder_16 (.a(bit_extender_1_out), .b(16'hf), .out(adder_16_out));  // open: cin, cout
  ROM #(.addrWidth(16), .Select("high")) rom_9 (.addr(adder_9_out), .data(out_4), .sel(Sel));
  ROM #(.addrWidth(16), .Select("high")) rom_10 (.addr(adder_10_out), .data(out_6), .sel(Sel));
  ROM #(.addrWidth(16), .Select("high")) rom_11 (.addr(adder_11_out), .data(out_8), .sel(Sel));
  ROM #(.addrWidth(16), .Select("high")) rom_12 (.addr(adder_12_out), .data(out_10), .sel(Sel));
  ROM #(.addrWidth(16), .Select("high")) rom_13 (.addr(adder_13_out), .data(out_12), .sel(Sel));
  ROM #(.addrWidth(16), .Select("high")) rom_14 (.addr(adder_14_out), .data(out_14), .sel(Sel));
  ROM #(.addrWidth(16), .Select("high")) rom_15 (.addr(adder_15_out), .data(out_16), .sel(Sel));
  ROM #(.addrWidth(16), .Select("high")) rom_16 (.addr(adder_16_out), .data(out_18), .sel(Sel));

  // Other names for the same wires on the sheet: Code[7:0] = ASCII_CODE; row1[7:0] = out_3; row2[7:0] = out_4;
  //   row3[7:0] = out_5; row4[7:0] = out_6; row5[7:0] = out_7; row6[7:0] = out_8; row7[7:0] = out_9;
  //   row8[7:0] = out_10; row9[7:0] = out_11; row10[7:0] = out_12; row11[7:0] = out_13; row12[7:0] = out_14;
  //   row13[7:0] = out_15; row14[7:0] = out_16; row15[7:0] = out_17; row16[7:0] = out_18

  // Notes on the sheet:
  //   ASCII字库地址
  //   contents of rom_1 (hex, n*v repeats v):
  //   0 0 63 63 73 7b 7f 6f 67 63 63 63 6*0 f 6*6 66 66 3c 6*0 9*63 3e 6*0 1e 33 61 4*60 61 33 1e 6*0 3e
  //   63 63 30 1c 6 3 63 63 3e 6*0 63 63 73 7b 7f 6f 67 63 63 63 6*0 f 6*6 66 66 3c 6*0 9*63 3e
  //   contents of rom_2 (hex, n*v repeats v):
  //   0 0 63 63 73 7b 7f 6f 67 63 63 63 6*0 f 6*6 66 66 3c 6*0 9*63 3e 6*0 1e 33 61 4*60 61 33 1e 6*0 3e
  //   63 63 30 1c 6 3 63 63 3e 6*0 63 63 73 7b 7f 6f 67 63 63 63 6*0 f 6*6 66 66 3c 6*0 9*63 3e
  //   contents of rom_3 (hex, n*v repeats v):
  //   0 0 63 63 73 7b 7f 6f 67 63 63 63 6*0 f 6*6 66 66 3c 6*0 9*63 3e 6*0 1e 33 61 4*60 61 33 1e 6*0 3e
  //   63 63 30 1c 6 3 63 63 3e 6*0 63 63 73 7b 7f 6f 67 63 63 63 6*0 f 6*6 66 66 3c 6*0 9*63 3e
  //   contents of rom_4 (hex, n*v repeats v):
  //   0 0 63 63 73 7b 7f 6f 67 63 63 63 6*0 f 6*6 66 66 3c 6*0 9*63 3e 6*0 1e 33 61 4*60 61 33 1e 6*0 3e
  //   63 63 30 1c 6 3 63 63 3e 6*0 63 63 73 7b 7f 6f 67 63 63 63 6*0 f 6*6 66 66 3c 6*0 9*63 3e
  //   contents of rom_5 (hex, n*v repeats v):
  //   0 0 63 63 73 7b 7f 6f 67 63 63 63 6*0 f 6*6 66 66 3c 6*0 9*63 3e 6*0 1e 33 61 4*60 61 33 1e 6*0 3e
  //   63 63 30 1c 6 3 63 63 3e 6*0 63 63 73 7b 7f 6f 67 63 63 63 6*0 f 6*6 66 66 3c 6*0 9*63 3e
  //   contents of rom_6 (hex, n*v repeats v):
  //   0 0 63 63 73 7b 7f 6f 67 63 63 63 6*0 f 6*6 66 66 3c 6*0 9*63 3e 6*0 1e 33 61 4*60 61 33 1e 6*0 3e
  //   63 63 30 1c 6 3 63 63 3e 6*0 63 63 73 7b 7f 6f 67 63 63 63 6*0 f 6*6 66 66 3c 6*0 9*63 3e
  //   contents of rom_7 (hex, n*v repeats v):
  //   0 0 63 63 73 7b 7f 6f 67 63 63 63 6*0 f 6*6 66 66 3c 6*0 9*63 3e 6*0 1e 33 61 4*60 61 33 1e 6*0 3e
  //   63 63 30 1c 6 3 63 63 3e 6*0 63 63 73 7b 7f 6f 67 63 63 63 6*0 f 6*6 66 66 3c 6*0 9*63 3e
  //   contents of rom_8 (hex, n*v repeats v):
  //   0 0 63 63 73 7b 7f 6f 67 63 63 63 6*0 f 6*6 66 66 3c 6*0 9*63 3e 6*0 1e 33 61 4*60 61 33 1e 6*0 3e
  //   63 63 30 1c 6 3 63 63 3e 6*0 63 63 73 7b 7f 6f 67 63 63 63 6*0 f 6*6 66 66 3c 6*0 9*63 3e
  //   contents of rom_9 (hex, n*v repeats v):
  //   0 0 63 63 73 7b 7f 6f 67 63 63 63 6*0 f 6*6 66 66 3c 6*0 9*63 3e 6*0 1e 33 61 4*60 61 33 1e 6*0 3e
  //   63 63 30 1c 6 3 63 63 3e 6*0 63 63 73 7b 7f 6f 67 63 63 63 6*0 f 6*6 66 66 3c 6*0 9*63 3e
  //   contents of rom_10 (hex, n*v repeats v):
  //   0 0 63 63 73 7b 7f 6f 67 63 63 63 6*0 f 6*6 66 66 3c 6*0 9*63 3e 6*0 1e 33 61 4*60 61 33 1e 6*0 3e
  //   63 63 30 1c 6 3 63 63 3e 6*0 63 63 73 7b 7f 6f 67 63 63 63 6*0 f 6*6 66 66 3c 6*0 9*63 3e
  //   contents of rom_11 (hex, n*v repeats v):
  //   0 0 63 63 73 7b 7f 6f 67 63 63 63 6*0 f 6*6 66 66 3c 6*0 9*63 3e 6*0 1e 33 61 4*60 61 33 1e 6*0 3e
  //   63 63 30 1c 6 3 63 63 3e 6*0 63 63 73 7b 7f 6f 67 63 63 63 6*0 f 6*6 66 66 3c 6*0 9*63 3e
  //   contents of rom_12 (hex, n*v repeats v):
  //   0 0 63 63 73 7b 7f 6f 67 63 63 63 6*0 f 6*6 66 66 3c 6*0 9*63 3e 6*0 1e 33 61 4*60 61 33 1e 6*0 3e
  //   63 63 30 1c 6 3 63 63 3e 6*0 63 63 73 7b 7f 6f 67 63 63 63 6*0 f 6*6 66 66 3c 6*0 9*63 3e
  //   contents of rom_13 (hex, n*v repeats v):
  //   0 0 63 63 73 7b 7f 6f 67 63 63 63 6*0 f 6*6 66 66 3c 6*0 9*63 3e 6*0 1e 33 61 4*60 61 33 1e 6*0 3e
  //   63 63 30 1c 6 3 63 63 3e 6*0 63 63 73 7b 7f 6f 67 63 63 63 6*0 f 6*6 66 66 3c 6*0 9*63 3e
  //   contents of rom_14 (hex, n*v repeats v):
  //   0 0 63 63 73 7b 7f 6f 67 63 63 63 6*0 f 6*6 66 66 3c 6*0 9*63 3e 6*0 1e 33 61 4*60 61 33 1e 6*0 3e
  //   63 63 30 1c 6 3 63 63 3e 6*0 63 63 73 7b 7f 6f 67 63 63 63 6*0 f 6*6 66 66 3c 6*0 9*63 3e
  //   contents of rom_15 (hex, n*v repeats v):
  //   0 0 63 63 73 7b 7f 6f 67 63 63 63 6*0 f 6*6 66 66 3c 6*0 9*63 3e 6*0 1e 33 61 4*60 61 33 1e 6*0 3e
  //   63 63 30 1c 6 3 63 63 3e 6*0 63 63 73 7b 7f 6f 67 63 63 63 6*0 f 6*6 66 66 3c 6*0 9*63 3e
  //   contents of rom_16 (hex, n*v repeats v):
  //   0 0 63 63 73 7b 7f 6f 67 63 63 63 6*0 f 6*6 66 66 3c 6*0 9*63 3e 6*0 1e 33 61 4*60 61 33 1e 6*0 3e
  //   63 63 30 1c 6 3 63 63 3e 6*0 63 63 73 7b 7f 6f 67 63 63 63 6*0 f 6*6 66 66 3c 6*0 9*63 3e
endmodule

module IFU (
  input  [31:0] Initial_Address,
  input  [31:0] Imm,
  input  [31:0] BusA,
  input  CLK,
  input  Reset,
  input  Halt,
  input  NxtASrc,
  input  NxtBSrc,
  output [31:0] PC,
  output [31:0] IR
);

  wire [31:0] adder_1_out, multiplexer_1_out, multiplexer_2_out, multiplexer_3_out;

  Register #(.width(32), .Select("low")) register_1 (
    .D(multiplexer_1_out), .Q(PC), .clk(CLK), .cs(Halt));  // open: en, clr, preset
  Multiplexer #(.width(32), .enable("false")) multiplexer_1 (
    .in0(adder_1_out), .in1(Initial_Address), .out(multiplexer_1_out), .sel(Reset));
  Multiplexer #(.width(32), .enable("false")) multiplexer_2 (
    .in0(PC), .in1(BusA), .out(multiplexer_2_out), .sel(NxtASrc));
  Multiplexer #(.width(32), .enable("false")) multiplexer_3 (
    .in0(32'h4), .in1(Imm), .out(multiplexer_3_out), .sel(NxtBSrc));
  Adder #(.width(32)) adder_1 (.a(multiplexer_2_out), .b(multiplexer_3_out), .out(adder_1_out));  // open: cin, cout
  ROM #(.addrWidth(16), .dataWidth(32), .Select("high")) \u_指令存储器  (.addr(PC[17:2]), .data(IR));

  // Other names for the same wires on the sheet: Init_Addr[31:0] = Initial_Address

  // Notes on the sheet:
  //   Halt: pull=down
  //   NxtASrc: pull=down
  //   Imm: pull=down
  //   BusA: pull=down
  //   NxtBSrc: pull=down
  //   指令存储器的数据位设置为32位，地址位设置为16位。存储器按照32位字长编址，地址位最低2位舍弃。
  //   输入信号
  //   输出信号
  //   contents of 指令存储器 (hex, n*v repeats v):
  //   100*0 12b7 fff28293 5de1863 288000ef 112623
endmodule

module \立即数扩展器  (
  input  [31:0] Instr,
  input  [2:0] Extop,
  output [31:0] imm
);

  wire [31:0] bit_extender_1_out, bit_extender_2_out, bit_extender_3_out, bit_extender_4_out;

  assign bit_extender_1_out = {{20{Instr[31]}}, Instr[31:20]};  // Bit_Extender bit_extender_1
  assign bit_extender_2_out = {{20{Instr[31]}}, {Instr[31:25], Instr[11:7]}};  // Bit_Extender bit_extender_2
  assign bit_extender_3_out = {{19{Instr[31]}}, {Instr[31], Instr[7], Instr[30:25], Instr[11:8], 1'b0}};  // Bit_Extender bit_extender_3
  assign bit_extender_4_out = {{11{Instr[31]}}, {Instr[31], Instr[19:12], Instr[20], Instr[30:21], 1'b0}};  // Bit_Extender bit_extender_4
  Multiplexer #(.select(3), .width(32), .enable("false")) multiplexer_1 (
    .in0(bit_extender_1_out), .in1({Instr[31:12], {12{1'b0}}}), .in2(bit_extender_2_out),
    .in3(bit_extender_3_out), .in4(bit_extender_4_out), .out(imm), .sel(Extop));  // open: in5, in6, in7

  // Notes on the sheet:
  //   Instr: pull=down
  //   Extop: pull=down
  //   输入引脚
  //   输出引脚
endmodule

module IDU (
  input  [31:0] IR,
  input  [31:0] BusW,
  input  [31:0] PC,
  input  [2:0] ExtOp,
  input  RegWr,
  input  ALUASrc,
  input  [1:0] ALUBSrc,
  input  in_8,
  output [31:0] DataA,
  output [31:0] DataB,
  output [31:0] BusA,
  output [6:0] OpCode,
  output [31:0] BusB,
  output [31:0] Imm,
  output [2:0] Funct3,
  output [6:0] Funct7
);

  \立即数扩展器  \u_立即数扩展器_1  (.Instr(IR), .Extop(ExtOp), .imm(Imm));
  RegFile regfile_1 (
    .R1_num(IR[19:15]), .R2_num(IR[24:20]), .Din(BusW), .Reg1Out(BusA), .Reg2Out(BusB),
    .Write_Reg_num(IR[11:7]), .Write_Enable(RegWr), .Clock(in_8));
  Multiplexer #(.width(32), .enable("false")) multiplexer_1 (.in0(BusA), .in1(PC), .out(DataA), .sel(ALUASrc));
  Multiplexer #(.select(2), .width(32), .enable("false")) multiplexer_2 (
    .in0(BusB), .in1(32'h4), .in2(Imm), .out(DataB), .sel(ALUBSrc));  // open: in3

  assign Funct3 = IR[14:12];
  assign Funct7 = IR[31:25];
  assign OpCode = IR[6:0];

  // Other names for the same wires on the sheet: clk = in_8; DataIn[31:0] = BusB; op[6:0] = IR[6:0]

  // Notes on the sheet:
  //   RegWr: pull=down
  //   ALUBSrc: pull=down
  //   ALUASrc: pull=down
  //   ExtOp: pull=down
  //   PC: pull=down
  //   BusW: pull=down
  //   指令解析
  //   输入信号
  //   访问寄存器堆
  //   输出信号
  //   输出数据
endmodule

module RegFile (
  input  [4:0] R1_num,
  input  [4:0] R2_num,
  input  [31:0] Din,
  input  [4:0] Write_Reg_num,
  input  Write_Enable,
  input  Clock,
  output [31:0] Reg1Out,
  output [31:0] Reg2Out
);

  wire and_1_out, and_2_out, and_3_out, and_4_out, and_5_out, and_6_out, and_7_out, and_8_out, and_9_out,
       and_10_out, and_11_out, and_12_out, and_13_out, and_14_out, and_15_out, and_16_out, and_17_out,
       and_18_out, and_19_out, and_20_out, and_21_out, and_22_out, and_23_out, and_24_out, and_25_out,
       and_26_out, and_27_out, and_28_out, and_29_out, and_30_out, and_31_out, and_32_out, and_33_out,
       and_34_out, and_35_out, and_36_out, decoder_1_out0, decoder_1_out1, decoder_1_out2, decoder_1_out3,
       decoder_2_out0, decoder_2_out1, decoder_2_out2, decoder_2_out3, decoder_2_out4, decoder_2_out5,
       decoder_2_out6, decoder_2_out7, decoder_3_out0, decoder_3_out1, decoder_3_out2, decoder_3_out3,
       decoder_3_out4, decoder_3_out5, decoder_3_out6, decoder_3_out7, decoder_4_out0, decoder_4_out1,
       decoder_4_out2, decoder_4_out3, decoder_4_out4, decoder_4_out5, decoder_4_out6, decoder_4_out7,
       decoder_5_out0, decoder_5_out1, decoder_5_out2, decoder_5_out3, decoder_5_out4, decoder_5_out5,
       decoder_5_out7;
  wire [31:0] register_1_q, register_2_q, register_3_q, register_4_q, register_5_q, register_6_q,
       register_7_q, register_8_q, register_9_q, register_10_q, register_11_q, register_12_q, register_13_q,
       register_14_q, register_15_q, register_16_q, register_17_q, register_18_q, register_19_q,
       register_20_q, register_21_q, register_22_q, register_23_q, register_24_q, register_25_q,
       register_26_q, register_27_q, register_28_q, register_29_q, register_30_q, register_31_q,
       register_32_q;

  Decoder #(.select(2), .enable("false")) decoder_1 (
    .out0(decoder_1_out0), .out1(decoder_1_out1), .out2(decoder_1_out2), .out3(decoder_1_out3),
    .sel(Write_Reg_num[4:3]));
  Decoder #(.select(3), .enable("false")) decoder_2 (
    .out0(decoder_2_out0), .out1(decoder_2_out1), .out2(decoder_2_out2), .out3(decoder_2_out3),
    .out4(decoder_2_out4), .out5(decoder_2_out5), .out6(decoder_2_out6), .out7(decoder_2_out7),
    .sel(Write_Reg_num[2:0]));
  Decoder #(.select(3), .enable("false")) decoder_3 (
    .out0(decoder_3_out0), .out1(decoder_3_out1), .out2(decoder_3_out2), .out3(decoder_3_out3),
    .out4(decoder_3_out4), .out5(decoder_3_out5), .out6(decoder_3_out6), .out7(decoder_3_out7),
    .sel(Write_Reg_num[2:0]));
  Decoder #(.select(3), .enable("false")) decoder_4 (
    .out0(decoder_4_out0), .out1(decoder_4_out1), .out2(decoder_4_out2), .out3(decoder_4_out3),
    .out4(decoder_4_out4), .out5(decoder_4_out5), .out6(decoder_4_out6), .out7(decoder_4_out7),
    .sel(Write_Reg_num[2:0]));
  Decoder #(.select(3), .enable("false")) decoder_5 (
    .out0(decoder_5_out0), .out1(decoder_5_out1), .out2(decoder_5_out2), .out3(decoder_5_out3),
    .out4(decoder_5_out4), .out5(decoder_5_out5), .out6(decoder_5_out5), .out7(decoder_5_out7),
    .sel(Write_Reg_num[2:0]));
  and and_1 (and_1_out, Write_Enable, decoder_1_out0);
  and and_2 (and_2_out, decoder_1_out1, Write_Enable);
  and and_3 (and_3_out, decoder_1_out2, Write_Enable);
  and and_4 (and_4_out, decoder_1_out3, Write_Enable);
  and and_5 (and_5_out, decoder_2_out0, and_1_out);
  and and_6 (and_6_out, decoder_2_out1, and_1_out);
  and and_7 (and_7_out, decoder_2_out2, and_1_out);
  and and_8 (and_8_out, decoder_2_out3, and_1_out);
  and and_9 (and_9_out, decoder_2_out4, and_1_out);
  and and_10 (and_10_out, decoder_2_out5, and_1_out);
  and and_11 (and_11_out, decoder_2_out6, and_1_out);
  and and_12 (and_12_out, decoder_2_out7, and_1_out);
  and and_13 (and_13_out, decoder_3_out0, and_2_out);
  and and_14 (and_14_out, decoder_3_out1, and_2_out);
  and and_15 (and_15_out, decoder_3_out2, and_2_out);
  and and_16 (and_16_out, decoder_3_out3, and_2_out);
  and and_17 (and_17_out, decoder_3_out4, and_2_out);
  and and_18 (and_18_out, decoder_3_out5, and_2_out);
  and and_19 (and_19_out, decoder_3_out6, and_2_out);
  and and_20 (and_20_out, decoder_3_out7, and_2_out);
  and and_21 (and_21_out, decoder_4_out0, and_3_out);
  and and_22 (and_22_out, decoder_4_out1, and_3_out);
  and and_23 (and_23_out, decoder_4_out2, and_3_out);
  and and_24 (and_24_out, decoder_4_out3, and_3_out);
  and and_25 (and_25_out, decoder_4_out4, and_3_out);
  and and_26 (and_26_out, decoder_4_out5, and_3_out);
  and and_27 (and_27_out, decoder_4_out6, and_3_out);
  and and_28 (and_28_out, decoder_4_out7, and_3_out);
  and and_29 (and_29_out, decoder_5_out0, and_4_out);
  and and_30 (and_30_out, decoder_5_out1, and_4_out);
  and and_31 (and_31_out, decoder_5_out2, and_4_out);
  and and_32 (and_32_out, decoder_5_out3, and_4_out);
  and and_33 (and_33_out, decoder_5_out4, and_4_out);
  and and_34 (and_34_out, decoder_5_out5, and_4_out);
  and and_35 (and_35_out, decoder_5_out5, and_4_out);
  and and_36 (and_36_out, decoder_5_out7, and_4_out);
  Register #(.width(32), .Select("low")) register_1 (.en(and_5_out), .Q(register_1_q), .clk(Clock));  // open: D, clr
  Register #(.width(32), .Select("low")) register_2 (
    .D(Din), .en(and_6_out), .Q(register_2_q), .clk(Clock));  // open: clr
  Register #(.width(32), .Select("low")) register_3 (
    .D(Din), .en(and_7_out), .Q(register_3_q), .clk(Clock));  // open: clr
  Register #(.width(32), .Select("low")) register_4 (
    .D(Din), .en(and_8_out), .Q(register_4_q), .clk(Clock));  // open: clr
  Register #(.width(32), .Select("low")) register_5 (.D(Din), .en(and_9_out), .Q(register_5_q));  // open: clk, clr
  Register #(.width(32), .Select("low")) register_6 (
    .D(Din), .en(and_10_out), .Q(register_6_q), .clk(Clock));  // open: clr
  Register #(.width(32), .Select("low")) register_7 (
    .D(Din), .en(and_11_out), .Q(register_7_q), .clk(Clock));  // open: clr
  Register #(.width(32), .Select("low")) register_8 (
    .D(Din), .en(and_12_out), .Q(register_8_q), .clk(Clock));  // open: clr
  Register #(.width(32), .Select("low")) register_9 (
    .D(Din), .en(and_13_out), .Q(register_9_q), .clk(Clock));  // open: clr
  Register #(.width(32), .Select("low")) register_10 (
    .D(Din), .en(and_14_out), .Q(register_10_q), .clk(Clock));  // open: clr
  Register #(.width(32), .Select("low")) register_11 (
    .D(Din), .en(and_15_out), .Q(register_11_q), .clk(Clock));  // open: clr
  Register #(.width(32), .Select("low")) register_12 (
    .D(Din), .en(and_16_out), .Q(register_12_q), .clk(Clock));  // open: clr
  Register #(.width(32), .Select("low")) register_13 (
    .D(Din), .en(and_17_out), .Q(register_13_q), .clk(Clock));  // open: clr
  Register #(.width(32), .Select("low")) register_14 (
    .D(Din), .en(and_18_out), .Q(register_14_q), .clk(Clock));  // open: clr
  Register #(.width(32), .Select("low")) register_15 (
    .D(Din), .en(and_19_out), .Q(register_15_q), .clk(Clock));  // open: clr
  Register #(.width(32), .Select("low")) register_16 (
    .D(Din), .en(and_20_out), .Q(register_16_q), .clk(Clock));  // open: clr
  Register #(.width(32), .Select("low")) register_17 (
    .D(Din), .en(and_21_out), .Q(register_17_q), .clk(Clock));  // open: clr
  Register #(.width(32), .Select("low")) register_18 (
    .D(Din), .en(and_22_out), .Q(register_18_q), .clk(Clock));  // open: clr
  Register #(.width(32), .Select("low")) register_19 (
    .D(Din), .en(and_23_out), .Q(register_19_q), .clk(Clock));  // open: clr
  Register #(.width(32), .Select("low")) register_20 (
    .D(Din), .en(and_24_out), .Q(register_20_q), .clk(Clock));  // open: clr
  Register #(.width(32), .Select("low")) register_21 (
    .D(Din), .en(and_25_out), .Q(register_21_q), .clk(Clock));  // open: clr
  Register #(.width(32), .Select("low")) register_22 (
    .D(Din), .en(and_26_out), .Q(register_22_q), .clk(Clock));  // open: clr
  Register #(.width(32), .Select("low")) register_23 (
    .D(Din), .en(and_27_out), .Q(register_23_q), .clk(Clock));  // open: clr
  Register #(.width(32), .Select("low")) register_24 (
    .D(Din), .en(and_28_out), .Q(register_24_q), .clk(Clock));  // open: clr
  Register #(.width(32), .Select("low")) register_25 (
    .D(Din), .en(and_29_out), .Q(register_25_q), .clk(Clock));  // open: clr
  Register #(.width(32), .Select("low")) register_26 (
    .D(Din), .en(and_30_out), .Q(register_26_q), .clk(Clock));  // open: clr
  Register #(.width(32), .Select("low")) register_27 (
    .D(Din), .en(and_31_out), .Q(register_27_q), .clk(Clock));  // open: clr
  Register #(.width(32), .Select("low")) register_28 (
    .D(Din), .en(and_32_out), .Q(register_28_q), .clk(Clock));  // open: clr
  Register #(.width(32), .Select("low")) register_29 (
    .D(Din), .en(and_33_out), .Q(register_29_q), .clk(Clock));  // open: clr
  Register #(.width(32), .Select("low")) register_30 (
    .D(Din), .en(and_34_out), .Q(register_30_q), .clk(Clock));  // open: clr
  Register #(.width(32), .Select("low")) register_31 (
    .D(Din), .en(and_35_out), .Q(register_31_q), .clk(Clock));  // open: clr
  Register #(.width(32), .Select("low")) register_32 (
    .D(Din), .en(and_36_out), .Q(register_32_q), .clk(Clock));  // open: clr
  Multiplexer #(.select(5), .width(32), .enable("false")) multiplexer_1 (
    .in0(register_1_q), .in1(register_2_q), .in2(register_3_q), .in3(register_4_q), .in4(register_5_q),
    .in5(register_6_q), .in6(register_7_q), .in7(register_8_q), .in8(register_9_q), .in9(register_10_q),
    .in10(register_11_q), .in11(register_12_q), .in12(register_13_q), .in13(register_14_q),
    .in14(register_15_q), .in15(register_16_q), .in16(register_17_q), .in17(register_18_q),
    .in18(register_19_q), .in19(register_20_q), .in20(register_21_q), .in21(register_22_q),
    .in22(register_23_q), .in23(register_24_q), .in24(register_25_q), .in25(register_26_q),
    .in26(register_27_q), .in27(register_28_q), .in28(register_29_q), .in29(register_30_q),
    .in30(register_31_q), .in31(register_32_q), .out(Reg1Out), .sel(R1_num));
  Multiplexer #(.select(5), .width(32), .enable("false")) multiplexer_2 (
    .in0(register_1_q), .in1(register_2_q), .in2(register_3_q), .in3(register_4_q), .in4(register_5_q),
    .in5(register_6_q), .in6(register_7_q), .in7(register_8_q), .in8(register_9_q), .in9(register_10_q),
    .in10(register_11_q), .in11(register_12_q), .in12(register_13_q), .in13(register_14_q),
    .in14(register_15_q), .in15(register_16_q), .in16(register_17_q), .in17(register_18_q),
    .in18(register_19_q), .in19(register_20_q), .in20(register_21_q), .in21(register_22_q),
    .in22(register_23_q), .in23(register_24_q), .in24(register_25_q), .in25(register_26_q),
    .in26(register_27_q), .in27(register_28_q), .in28(register_29_q), .in29(register_30_q),
    .in30(register_31_q), .in31(register_32_q), .out(Reg2Out), .sel(R2_num));

  // Other names for the same wires on the sheet: CLK = Clock; RA[4:0] = R1_num; RB[4:0] = R2_num; RDA[31:0] = Reg1Out;
  //   RDB[31:0] = Reg2Out; RW[4:0] = Write_Reg_num; WE = Write_Enable

  // Notes on the sheet:
  //   输入引脚
  //   电路功能：实现寄存器堆功能，实现0-31号寄存器。写使能有效且时钟边沿有效后写入数据，随时读出双口数据
  //   输出引脚
endmodule

module \数据存储器  (
  input  [15:0] Addr,
  input  [31:0] Din,
  input  CLK,
  input  CLR,
  input  [2:0] MemOp,
  input  WE,
  input  SEL,
  output [31:0] DataOut
);

  wire and_1_out, and_2_out, and_3_out, and_4_out, and_5_out, and_6_out, and_7_out, or_1_out, or_2_out;
  wire [7:0] ram_1_data, ram_2_data, ram_3_data, ram_4_data;
  wire [31:0] bit_extender_1_out, bit_extender_2_out, bit_extender_3_out, bit_extender_4_out;

  and and_1 (and_1_out, WE, and_2_out);
  and and_2 (and_2_out, ~MemOp[0], ~MemOp[1], ~MemOp[2]);  // AND_Gate
  and and_3 (and_3_out, ~MemOp[0], MemOp[1], MemOp[2]);  // AND_Gate
  and and_4 (and_4_out, MemOp[0], ~MemOp[1], MemOp[2]);  // AND_Gate
  RAM #(.addrWidth(16), .bus("separate"), .Select("high")) ram_1 (
    .addr(Addr), .din(Din[31:24]), .data(ram_1_data), .str(and_1_out), .sel(SEL), .clk(CLK), .clr(CLR));  // open: ld
  and and_5 (and_5_out, WE, and_2_out);
  RAM #(.addrWidth(16), .bus("separate"), .Select("high")) ram_2 (
    .addr(Addr), .din(Din[23:16]), .data(ram_2_data), .str(and_5_out), .sel(SEL), .clk(CLK), .clr(CLR));  // open: ld
  or or_1 (or_1_out, and_2_out, and_3_out);
  and and_6 (and_6_out, WE, or_1_out);
  RAM #(.addrWidth(16), .bus("separate"), .Select("high")) ram_3 (
    .addr(Addr), .din(Din[15:8]), .data(ram_3_data), .str(and_6_out), .sel(SEL), .clk(CLK), .clr(CLR));  // open: ld
  or or_2 (or_2_out, or_1_out, and_4_out);
  and and_7 (and_7_out, WE, or_2_out);
  RAM #(.addrWidth(16), .bus("separate"), .Select("high")) ram_4 (
    .addr(Addr), .din(Din[7:0]), .data(ram_4_data), .str(and_7_out), .sel(SEL), .clk(CLK), .clr(CLR));  // open: ld
  assign bit_extender_1_out = {{24{1'b0}}, ram_4_data};  // Bit_Extender bit_extender_1
  assign bit_extender_2_out = {{16{1'b0}}, {ram_3_data, ram_4_data}};  // Bit_Extender bit_extender_2
  assign bit_extender_3_out = {{24{ram_4_data[7]}}, ram_4_data};  // Bit_Extender bit_extender_3
  assign bit_extender_4_out = {{16{ram_3_data[7]}}, {ram_3_data, ram_4_data}};  // Bit_Extender bit_extender_4
  Multiplexer #(.select(3), .width(32), .enable("false")) multiplexer_1 (
    .in0({ram_1_data, ram_2_data, ram_3_data, ram_4_data}), .in1(bit_extender_1_out),
    .in2(bit_extender_2_out), .in5(bit_extender_3_out), .in6(bit_extender_4_out), .out(DataOut), .sel(MemOp));  // open: in3, in4, in7

  // Other names for the same wires on the sheet: Dout[31:0] = DataOut

  // Notes on the sheet:
  //   输入引脚区
  //   32位数据存储器，按字节分4片存储，可按照字节、半字和字进行存储；读取字节或半字时，支持0扩展和符号位扩展。
  //   为了后续实验中的引用，不要修改MemOp的编码定义，以及引脚名称和在布局图中位置。
  //   输出引脚区
endmodule

module DataPath (
  input  [2:0] ExtOp,
  input  [2:0] MemOp,
  input  RegWr,
  input  ALUASrc,
  input  MemWr,
  input  [1:0] ALUBSrc,
  input  [31:0] Initial_Address,
  input  [3:0] ALUctr,
  input  MemToReg,
  input  [2:0] Branch,
  input  Halt,
  output [6:0] OpCode,
  output [2:0] Funct3,
  output [6:0] Funct7
);

  wire alu_1_p5, branch_1_nxtasrc, branch_1_nxtbsrc, clk, RESET;
  wire [31:0] alu_1_p4, idu_1_busa, idu_1_busb, idu_1_dataa, idu_1_datab, idu_1_imm, ifu_1_pc,
       multiplexer_1_out, \指令存储器_data , \数据存储器_1_dataout ;

  Clock clock_1 (.out(clk));
  Button u_Reset (.out(RESET));
  IFU ifu_1 (
    .PC(ifu_1_pc), .Initial_Address(Initial_Address), .BusA(idu_1_busa), .Halt(Halt),
    .NxtASrc(branch_1_nxtasrc), .NxtBSrc(branch_1_nxtbsrc), .Imm(idu_1_imm), .CLK(clk), .Reset(RESET));  // open: IR
  ROM #(.addrWidth(16), .dataWidth(32), .Select("high")) \u_指令存储器  (.addr(ifu_1_pc[17:2]), .data(\指令存储器_data ));
  IDU idu_1 (
    .ExtOp(ExtOp), .RegWr(RegWr), .OpCode(OpCode), .ALUASrc(ALUASrc), .ALUBSrc(ALUBSrc), .Funct3(Funct3),
    .Funct7(Funct7), .IR(\指令存储器_data ), .BusW(multiplexer_1_out), .PC(ifu_1_pc), .DataA(idu_1_dataa),
    .BusB(idu_1_busb), .DataB(idu_1_datab), .Imm(idu_1_imm), .BusA(idu_1_busa), .in_8(clk));
  // ALU alu_1: pin names not known; wires that end beside it: idu_1_dataa, idu_1_datab, ALUctr, alu_1_p4, alu_1_p5
  Branch branch_1 (
    .Branch(Branch), .NxtASrc(branch_1_nxtasrc), .Zero(alu_1_p5), .NxtBSrc(branch_1_nxtbsrc),
    .Result0(alu_1_p4[0]));
  \数据存储器  \u_数据存储器_1  (
    .Addr(alu_1_p4[17:2]), .Din(idu_1_busb), .DataOut(\数据存储器_1_dataout ), .CLK(clk), .MemOp(MemOp), .WE(MemWr));  // open: CLR, SEL
  Multiplexer #(.width(32), .enable("false")) multiplexer_1 (
    .in0(alu_1_p4), .in1(\数据存储器_1_dataout ), .out(multiplexer_1_out), .sel(MemToReg));

  // Other names for the same wires on the sheet: Init_Addr[31:0] = Initial_Address; op[6:0] = OpCode

  // Notes on the sheet:
  //   Halt: pull=down
  //   RegWr: pull=down
  //   ALUASrc: pull=down
  //   ALUctr: pull=down
  //   ExtOp: pull=down
  //   ALUBSrc: pull=down
  //   Branch: pull=down
  //   contents of 指令存储器 (hex, n*v repeats v):
  //   fffff2b7 6428293 502023 4032d313 602223 401383 fff3c413 802423 7424b3 902623 fc049ce3 3000567 a02823
  //   64597
  //   输入信号
  //   数据通路设计，提示指令存储器和数据存储器数据位32位，编址以字为单位，地址信号低2位舍弃。
  //   ALU
  //   输出信号
endmodule

module Branch (
  input  [2:0] Branch,
  input  Zero,
  input  Result0,
  output NxtASrc,
  output NxtBSrc
);

  wire not_1_out, or_1_out;

  not not_1 (not_1_out, Zero);
  or or_1 (or_1_out, Zero, ~Result0);  // OR_Gate
  and and_1 (NxtASrc, Branch[1], ~Branch[2]);  // AND_Gate
  Multiplexer #(.select(3), .enable("false")) multiplexer_1 (
    .in0(1'b0), .in1(1'b1), .in2(1'b1), .in4(Zero), .in5(not_1_out), .in6(Result0), .in7(or_1_out),
    .out(NxtBSrc), .sel(Branch));  // open: in3

  // Notes on the sheet:
  //   Zero: pull=down
  //   Branch: pull=down
  //   输入信号
  //   输出信号
endmodule

module ascii (
  input  [7:0] ASCII_CODE,
  input  Sel,
  output [7:0] out_3,
  output [7:0] out_4,
  output [7:0] out_5,
  output [7:0] out_6,
  output [7:0] out_7,
  output [7:0] out_8,
  output [7:0] out_9,
  output [7:0] out_10,
  output [7:0] out_11,
  output [7:0] out_12,
  output [7:0] out_13,
  output [7:0] out_14,
  output [7:0] out_15,
  output [7:0] out_16,
  output [7:0] out_17,
  output [7:0] out_18
);

  wire [15:0] adder_1_out, adder_2_out, adder_3_out, adder_4_out, adder_5_out, adder_6_out, adder_7_out,
       adder_8_out, adder_9_out, adder_10_out, adder_11_out, adder_12_out, adder_13_out, adder_14_out,
       adder_15_out, adder_16_out, bit_extender_1_out, shifter_1_out;

  assign bit_extender_1_out = {{8{1'b0}}, ASCII_CODE};  // Bit_Extender bit_extender_1
  Shifter #(.width(16)) shifter_1 (.in(bit_extender_1_out), .\dist (4'b0100), .out(shifter_1_out));
  Adder #(.width(16)) adder_1 (.a(shifter_1_out), .b({16{1'b0}}), .out(adder_1_out));  // open: cin, cout
  Adder #(.width(16)) adder_2 (.a(shifter_1_out), .b(16'h2), .out(adder_2_out));  // open: cin, cout
  Adder #(.width(16)) adder_3 (.a(shifter_1_out), .b(16'h4), .out(adder_3_out));  // open: cin, cout
  Adder #(.width(16)) adder_4 (.a(shifter_1_out), .b(16'h6), .out(adder_4_out));  // open: cin, cout
  Adder #(.width(16)) adder_5 (.a(shifter_1_out), .b(16'h8), .out(adder_5_out));  // open: cin, cout
  Adder #(.width(16)) adder_6 (.a(shifter_1_out), .b(16'ha), .out(adder_6_out));  // open: cin, cout
  Adder #(.width(16)) adder_7 (.a(shifter_1_out), .b(16'hc), .out(adder_7_out));  // open: cin, cout
  Adder #(.width(16)) adder_8 (.a(shifter_1_out), .b(16'he), .out(adder_8_out));  // open: cin, cout
  ROM #(.addrWidth(16), .Select("high")) rom_1 (.addr(adder_1_out), .data(out_3), .sel(Sel));
  ROM #(.addrWidth(16), .Select("high")) rom_2 (.addr(adder_2_out), .data(out_7), .sel(Sel));
  ROM #(.addrWidth(16), .Select("high")) rom_3 (.addr(adder_3_out), .data(out_11), .sel(Sel));
  ROM #(.addrWidth(16), .Select("high")) rom_4 (.addr(adder_4_out), .data(out_15), .sel(Sel));
  ROM #(.addrWidth(16), .Select("high")) rom_5 (.addr(adder_5_out), .data(out_4), .sel(Sel));
  ROM #(.addrWidth(16), .Select("high")) rom_6 (.addr(adder_6_out), .data(out_8), .sel(Sel));
  ROM #(.addrWidth(16), .Select("high")) rom_7 (.addr(adder_7_out), .data(out_12), .sel(Sel));
  ROM #(.addrWidth(16), .Select("high")) rom_8 (.addr(adder_8_out), .data(out_16), .sel(Sel));
  DotMatrix #(.inputtype("row"), .matrixcols(8), .matrixrows(16)) dotmatrix_1 (
    .row0(out_3), .row1(out_5), .row2(out_7), .row3(out_9), .row4(out_11), .row5(out_13), .row6(out_15),
    .row7(out_17), .row8(out_4), .row9(out_6), .row10(out_8), .row11(out_10), .row12(out_12), .row13(out_14),
    .row14(out_16), .row15(out_18));
  Adder #(.width(16)) adder_9 (.a(shifter_1_out), .b(16'h1), .out(adder_9_out));  // open: cin, cout
  Adder #(.width(16)) adder_10 (.a(shifter_1_out), .b(16'h3), .out(adder_10_out));  // open: cin, cout
  Adder #(.width(16)) adder_11 (.a(shifter_1_out), .b(16'h5), .out(adder_11_out));  // open: cin, cout
  Adder #(.width(16)) adder_12 (.a(shifter_1_out), .b(16'h7), .out(adder_12_out));  // open: cin, cout
  Adder #(.width(16)) adder_13 (.a(shifter_1_out), .b(16'h9), .out(adder_13_out));  // open: cin, cout
  Adder #(.width(16)) adder_14 (.a(shifter_1_out), .b(16'hb), .out(adder_14_out));  // open: cin, cout
  Adder #(.width(16)) adder_15 (.a(shifter_1_out), .b(16'hd), .out(adder_15_out));  // open: cin, cout
  Adder #(.width(16)) adder_16 (.a(shifter_1_out), .b(16'hf), .out(adder_16_out));  // open: cin, cout
  ROM #(.addrWidth(16), .Select("high")) rom_9 (.addr(adder_9_out), .data(out_5), .sel(Sel));
  ROM #(.addrWidth(16), .Select("high")) rom_10 (.addr(adder_10_out), .data(out_9), .sel(Sel));
  ROM #(.addrWidth(16), .Select("high")) rom_11 (.addr(adder_11_out), .data(out_13), .sel(Sel));
  ROM #(.addrWidth(16), .Select("high")) rom_12 (.addr(adder_12_out), .data(out_17), .sel(Sel));
  ROM #(.addrWidth(16), .Select("high")) rom_13 (.addr(adder_13_out), .data(out_6), .sel(Sel));
  ROM #(.addrWidth(16), .Select("high")) rom_14 (.addr(adder_14_out), .data(out_10), .sel(Sel));
  ROM #(.addrWidth(16), .Select("high")) rom_15 (.addr(adder_15_out), .data(out_14), .sel(Sel));
  ROM #(.addrWidth(16), .Select("high")) rom_16 (.addr(adder_16_out), .data(out_18), .sel(Sel));

  // Other names for the same wires on the sheet: Code[7:0] = ASCII_CODE; row1[7:0] = out_3; row2[7:0] = out_5;
  //   row3[7:0] = out_7; row4[7:0] = out_9; row5[7:0] = out_11; row6[7:0] = out_13; row7[7:0] = out_15;
  //   row8[7:0] = out_17; row9[7:0] = out_4; row10[7:0] = out_6; row11[7:0] = out_8; row12[7:0] = out_10;
  //   row13[7:0] = out_12; row14[7:0] = out_14; row15[7:0] = out_16; row16[7:0] = out_18

  // Notes on the sheet:
  //   ASCII字库地址
  //   contents of rom_1 (hex, n*v repeats v):
  //   18*0 18 3c 3c 3c 18 18 18 0 18 18 5*0 63 63 63 22 14*0 36 36 7f 36 36 36 7f 36 36 4*0 c c 3e 63 61
  //   60 3e 3 3 43 63 3e c c 7*0 61 63 6 c 18 33 63 7*0 1c 36 36 1c 3b 6e 66 66 3b 5*0 30 30 30 60 13*0 c
  //   18 18 4*30 18 18 c 6*0 18 c c 4*6 c c 18 8*0 42 66 3c ff 3c 66 42 9*0 18 18 18 ff 18 18 18 15*0 18
  //   18 18 30 9*0 ff 18*0 18 18 6*0 1 3 7 e 1c 38 70 e0 c0 80 6*0 3e 63 63 63 6b 6b 63 63 63 3e 6*0 c 1c
  //   3c 6*c 3f 6*0 3e 63 3 6 c 18 30 61 63 7f 6*0 3e 63 3 3 1e 3 3 3 63 3e 6*0 6 e 1e 36 66 66 7f 6 6 f
  //   6*0 7f 60 60 60 7e 3 3 63 73 3e 6*0 1c 30 60 60 7e 4*63 3e 6*0 7f 63 3 6 6 c c 18 18 18 6*0 3e 63 63
  //   63 3e 4*63 3e 6*0 3e 4*63 3f 3 3 6 3c 9*0 18 18 0 0 0 18 18 9*0 18 18 0 0 0 18 18 18 30 5*0 6 c 18
  //   30 60 30 18 c 6 10*0 7e 0 0 7e 9*0 60 30 18 c 6 c 18 30 60 6*0 3e 63 63 6 c c c 0 c c 6*0 3e 63 63
  //   6f 6b 6b 6e 60 60 3e 6*0 8 1c 36 63 63 63 7f 63 63 63 6*0 7e 33 33 33 3e 4*33 7e 6*0 1e 33 61 4*60
  //   61 33 1e 6*0 7c 36 6*33 36 7c 6*0 7f 33 31 34 3c 34 30 31 33 7f 6*0 7f 33 31 34 3c 34 30 30 30 78
  //   6*0 1e 33 61 60 60 6f 63 63 37 1d 6*0 4*63 7f 5*63 6*0 3c 8*18 3c 6*0 f 6*6 66 66 3c 6*0 73 33 36 36
  //   3c 36 36 33 33 73 6*0 78 6*30 31 33 7f 6*0 63 77 7f 6b 6*63 6*0 63 63 73 7b 7f 6f 67 63 63 63 6*0 1c
  //   36 6*63 36 1c 6*0 7e 33 33 33 3e 4*30 78 6*0 3e 6*63 6b 6f 3e 6 7 4*0 7e 33 33 33 3e 36 36 33 33 73
  //   6*0 3e 63 63 30 1c 6 3 63 63 3e 6*0 ff db 99 6*18 3c 6*0 9*63 3e 6*0 7*63 36 1c 8 6*0 5*63 6b 6b 7f
  //   36 36 6*0 c3 c3 66 3c 18 18 3c 66 c3 c3 6*0 c3 c3 c3 66 3c 4*18 3c 6*0 7f 63 43 6 c 18 30 61 63 7f
  //   6*0 3c 8*30 3c 6*0 80 c0 e0 70 38 1c e 7 3 1 6*0 3c 8*c 3c 4*0 8 1c 36 63 24*0 ff 0 0 0 18 18 c 18*0
  //   3c 46 6 3e 66 66 3b 6*0 70 30 30 3c 36 4*33 6e 9*0 3e 63 60 60 60 63 3e 6*0 e 6 6 1e 36 4*66 3b 9*0
  //   3e 63 63 7e 60 63 3e 6*0 1c 36 32 30 7c 4*30 78 9*0 3b 4*66 3e 6 66 3c 4*0 70 30 30 36 3b 4*33 73
  //   6*0 c c 0 1c 5*c 1e 6*0 6 6 0 e 5*6 66 66 3c 4*0 70 30 30 33 33 36 3c 36 33 73 6*0 1c 8*c 1e 9*0 6e
  //   7f 5*6b 9*0 6e 6*33 9*0 3e 5*63 3e 9*0 6e 4*33 3e 30 30 78 7*0 3b 4*66 3e 6 6 f 7*0 6e 3b 33 30 30
  //   30 78 9*0 3e 63 38 e 3 63 3e 6*0 8 18 18 7e 4*18 1b e 9*0 6*66 3b 9*0 63 63 36 36 1c 1c 8 9*0 63 63
  //   63 6b 6b 7f 36 9*0 63 36 1c 1c 1c 36 63 9*0 5*63 3f 3 6 3c 7*0 7f 66 c 18 30 63 7f 6*0 e 18 18 18 70
  //   4*18 e 6*0 5*18 0 5*18 5*0 70 18 18 18 e 4*18 70 6*0 3b 6e 13*0 70 d8 d8 70
  //   contents of rom_2 (hex, n*v repeats v):
  //   18*0 18 3c 3c 3c 18 18 18 0 18 18 5*0 63 63 63 22 14*0 36 36 7f 36 36 36 7f 36 36 4*0 c c 3e 63 61
  //   60 3e 3 3 43 63 3e c c 7*0 61 63 6 c 18 33 63 7*0 1c 36 36 1c 3b 6e 66 66 3b 5*0 30 30 30 60 13*0 c
  //   18 18 4*30 18 18 c 6*0 18 c c 4*6 c c 18 8*0 42 66 3c ff 3c 66 42 9*0 18 18 18 ff 18 18 18 15*0 18
  //   18 18 30 9*0 ff 18*0 18 18 6*0 1 3 7 e 1c 38 70 e0 c0 80 6*0 3e 63 63 63 6b 6b 63 63 63 3e 6*0 c 1c
  //   3c 6*c 3f 6*0 3e 63 3 6 c 18 30 61 63 7f 6*0 3e 63 3 3 1e 3 3 3 63 3e 6*0 6 e 1e 36 66 66 7f 6 6 f
  //   6*0 7f 60 60 60 7e 3 3 63 73 3e 6*0 1c 30 60 60 7e 4*63 3e 6*0 7f 63 3 6 6 c c 18 18 18 6*0 3e 63 63
  //   63 3e 4*63 3e 6*0 3e 4*63 3f 3 3 6 3c 9*0 18 18 0 0 0 18 18 9*0 18 18 0 0 0 18 18 18 30 5*0 6 c 18
  //   30 60 30 18 c 6 10*0 7e 0 0 7e 9*0 60 30 18 c 6 c 18 30 60 6*0 3e 63 63 6 c c c 0 c c 6*0 3e 63 63
  //   6f 6b 6b 6e 60 60 3e 6*0 8 1c 36 63 63 63 7f 63 63 63 6*0 7e 33 33 33 3e 4*33 7e 6*0 1e 33 61 4*60
  //   61 33 1e 6*0 7c 36 6*33 36 7c 6*0 7f 33 31 34 3c 34 30 31 33 7f 6*0 7f 33 31 34 3c 34 30 30 30 78
  //   6*0 1e 33 61 60 60 6f 63 63 37 1d 6*0 4*63 7f 5*63 6*0 3c 8*18 3c 6*0 f 6*6 66 66 3c 6*0 73 33 36 36
  //   3c 36 36 33 33 73 6*0 78 6*30 31 33 7f 6*0 63 77 7f 6b 6*63 6*0 63 63 73 7b 7f 6f 67 63 63 63 6*0 1c
  //   36 6*63 36 1c 6*0 7e 33 33 33 3e 4*30 78 6*0 3e 6*63 6b 6f 3e 6 7 4*0 7e 33 33 33 3e 36 36 33 33 73
  //   6*0 3e 63 63 30 1c 6 3 63 63 3e 6*0 ff db 99 6*18 3c 6*0 9*63 3e 6*0 7*63 36 1c 8 6*0 5*63 6b 6b 7f
  //   36 36 6*0 c3 c3 66 3c 18 18 3c 66 c3 c3 6*0 c3 c3 c3 66 3c 4*18 3c 6*0 7f 63 43 6 c 18 30 61 63 7f
  //   6*0 3c 8*30 3c 6*0 80 c0 e0 70 38 1c e 7 3 1 6*0 3c 8*c 3c 4*0 8 1c 36 63 24*0 ff 0 0 0 18 18 c 18*0
  //   3c 46 6 3e 66 66 3b 6*0 70 30 30 3c 36 4*33 6e 9*0 3e 63 60 60 60 63 3e 6*0 e 6 6 1e 36 4*66 3b 9*0
  //   3e 63 63 7e 60 63 3e 6*0 1c 36 32 30 7c 4*30 78 9*0 3b 4*66 3e 6 66 3c 4*0 70 30 30 36 3b 4*33 73
  //   6*0 c c 0 1c 5*c 1e 6*0 6 6 0 e 5*6 66 66 3c 4*0 70 30 30 33 33 36 3c 36 33 73 6*0 1c 8*c 1e 9*0 6e
  //   7f 5*6b 9*0 6e 6*33 9*0 3e 5*63 3e 9*0 6e 4*33 3e 30 30 78 7*0 3b 4*66 3e 6 6 f 7*0 6e 3b 33 30 30
  //   30 78 9*0 3e 63 38 e 3 63 3e 6*0 8 18 18 7e 4*18 1b e 9*0 6*66 3b 9*0 63 63 36 36 1c 1c 8 9*0 63 63
  //   63 6b 6b 7f 36 9*0 63 36 1c 1c 1c 36 63 9*0 5*63 3f 3 6 3c 7*0 7f 66 c 18 30 63 7f 6*0 e 18 18 18 70
  //   4*18 e 6*0 5*18 0 5*18 5*0 70 18 18 18 e 4*18 70 6*0 3b 6e 13*0 70 d8 d8 70
  //   contents of rom_3 (hex, n*v repeats v):
  //   18*0 18 3c 3c 3c 18 18 18 0 18 18 5*0 63 63 63 22 14*0 36 36 7f 36 36 36 7f 36 36 4*0 c c 3e 63 61
  //   60 3e 3 3 43 63 3e c c 7*0 61 63 6 c 18 33 63 7*0 1c 36 36 1c 3b 6e 66 66 3b 5*0 30 30 30 60 13*0 c
  //   18 18 4*30 18 18 c 6*0 18 c c 4*6 c c 18 8*0 42 66 3c ff 3c 66 42 9*0 18 18 18 ff 18 18 18 15*0 18
  //   18 18 30 9*0 ff 18*0 18 18 6*0 1 3 7 e 1c 38 70 e0 c0 80 6*0 3e 63 63 63 6b 6b 63 63 63 3e 6*0 c 1c
  //   3c 6*c 3f 6*0 3e 63 3 6 c 18 30 61 63 7f 6*0 3e 63 3 3 1e 3 3 3 63 3e 6*0 6 e 1e 36 66 66 7f 6 6 f
  //   6*0 7f 60 60 60 7e 3 3 63 73 3e 6*0 1c 30 60 60 7e 4*63 3e 6*0 7f 63 3 6 6 c c 18 18 18 6*0 3e 63 63
  //   63 3e 4*63 3e 6*0 3e 4*63 3f 3 3 6 3c 9*0 18 18 0 0 0 18 18 9*0 18 18 0 0 0 18 18 18 30 5*0 6 c 18
  //   30 60 30 18 c 6 10*0 7e 0 0 7e 9*0 60 30 18 c 6 c 18 30 60 6*0 3e 63 63 6 c c c 0 c c 6*0 3e 63 63
  //   6f 6b 6b 6e 60 60 3e 6*0 8 1c 36 63 63 63 7f 63 63 63 6*0 7e 33 33 33 3e 4*33 7e 6*0 1e 33 61 4*60
  //   61 33 1e 6*0 7c 36 6*33 36 7c 6*0 7f 33 31 34 3c 34 30 31 33 7f 6*0 7f 33 31 34 3c 34 30 30 30 78
  //   6*0 1e 33 61 60 60 6f 63 63 37 1d 6*0 4*63 7f 5*63 6*0 3c 8*18 3c 6*0 f 6*6 66 66 3c 6*0 73 33 36 36
  //   3c 36 36 33 33 73 6*0 78 6*30 31 33 7f 6*0 63 77 7f 6b 6*63 6*0 63 63 73 7b 7f 6f 67 63 63 63 6*0 1c
  //   36 6*63 36 1c 6*0 7e 33 33 33 3e 4*30 78 6*0 3e 6*63 6b 6f 3e 6 7 4*0 7e 33 33 33 3e 36 36 33 33 73
  //   6*0 3e 63 63 30 1c 6 3 63 63 3e 6*0 ff db 99 6*18 3c 6*0 9*63 3e 6*0 7*63 36 1c 8 6*0 5*63 6b 6b 7f
  //   36 36 6*0 c3 c3 66 3c 18 18 3c 66 c3 c3 6*0 c3 c3 c3 66 3c 4*18 3c 6*0 7f 63 43 6 c 18 30 61 63 7f
  //   6*0 3c 8*30 3c 6*0 80 c0 e0 70 38 1c e 7 3 1 6*0 3c 8*c 3c 4*0 8 1c 36 63 24*0 ff 0 0 0 18 18 c 18*0
  //   3c 46 6 3e 66 66 3b 6*0 70 30 30 3c 36 4*33 6e 9*0 3e 63 60 60 60 63 3e 6*0 e 6 6 1e 36 4*66 3b 9*0
  //   3e 63 63 7e 60 63 3e 6*0 1c 36 32 30 7c 4*30 78 9*0 3b 4*66 3e 6 66 3c 4*0 70 30 30 36 3b 4*33 73
  //   6*0 c c 0 1c 5*c 1e 6*0 6 6 0 e 5*6 66 66 3c 4*0 70 30 30 33 33 36 3c 36 33 73 6*0 1c 8*c 1e 9*0 6e
  //   7f 5*6b 9*0 6e 6*33 9*0 3e 5*63 3e 9*0 6e 4*33 3e 30 30 78 7*0 3b 4*66 3e 6 6 f 7*0 6e 3b 33 30 30
  //   30 78 9*0 3e 63 38 e 3 63 3e 6*0 8 18 18 7e 4*18 1b e 9*0 6*66 3b 9*0 63 63 36 36 1c 1c 8 9*0 63 63
  //   63 6b 6b 7f 36 9*0 63 36 1c 1c 1c 36 63 9*0 5*63 3f 3 6 3c 7*0 7f 66 c 18 30 63 7f 6*0 e 18 18 18 70
  //   4*18 e 6*0 5*18 0 5*18 5*0 70 18 18 18 e 4*18 70 6*0 3b 6e 13*0 70 d8 d8 70
  //   contents of rom_4 (hex, n*v repeats v):
  //   18*0 18 3c 3c 3c 18 18 18 0 18 18 5*0 63 63 63 22 14*0 36 36 7f 36 36 36 7f 36 36 4*0 c c 3e 63 61
  //   60 3e 3 3 43 63 3e c c 7*0 61 63 6 c 18 33 63 7*0 1c 36 36 1c 3b 6e 66 66 3b 5*0 30 30 30 60 13*0 c
  //   18 18 4*30 18 18 c 6*0 18 c c 4*6 c c 18 8*0 42 66 3c ff 3c 66 42 9*0 18 18 18 ff 18 18 18 15*0 18
  //   18 18 30 9*0 ff 18*0 18 18 6*0 1 3 7 e 1c 38 70 e0 c0 80 6*0 3e 63 63 63 6b 6b 63 63 63 3e 6*0 c 1c
  //   3c 6*c 3f 6*0 3e 63 3 6 c 18 30 61 63 7f 6*0 3e 63 3 3 1e 3 3 3 63 3e 6*0 6 e 1e 36 66 66 7f 6 6 f
  //   6*0 7f 60 60 60 7e 3 3 63 73 3e 6*0 1c 30 60 60 7e 4*63 3e 6*0 7f 63 3 6 6 c c 18 18 18 6*0 3e 63 63
  //   63 3e 4*63 3e 6*0 3e 4*63 3f 3 3 6 3c 9*0 18 18 0 0 0 18 18 9*0 18 18 0 0 0 18 18 18 30 5*0 6 c 18
  //   30 60 30 18 c 6 10*0 7e 0 0 7e 9*0 60 30 18 c 6 c 18 30 60 6*0 3e 63 63 6 c c c 0 c c 6*0 3e 63 63
  //   6f 6b 6b 6e 60 60 3e 6*0 8 1c 36 63 63 63 7f 63 63 63 6*0 7e 33 33 33 3e 4*33 7e 6*0 1e 33 61 4*60
  //   61 33 1e 6*0 7c 36 6*33 36 7c 6*0 7f 33 31 34 3c 34 30 31 33 7f 6*0 7f 33 31 34 3c 34 30 30 30 78
  //   6*0 1e 33 61 60 60 6f 63 63 37 1d 6*0 4*63 7f 5*63 6*0 3c 8*18 3c 6*0 f 6*6 66 66 3c 6*0 73 33 36 36
  //   3c 36 36 33 33 73 6*0 78 6*30 31 33 7f 6*0 63 77 7f 6b 6*63 6*0 63 63 73 7b 7f 6f 67 63 63 63 6*0 1c
  //   36 6*63 36 1c 6*0 7e 33 33 33 3e 4*30 78 6*0 3e 6*63 6b 6f 3e 6 7 4*0 7e 33 33 33 3e 36 36 33 33 73
  //   6*0 3e 63 63 30 1c 6 3 63 63 3e 6*0 ff db 99 6*18 3c 6*0 9*63 3e 6*0 7*63 36 1c 8 6*0 5*63 6b 6b 7f
  //   36 36 6*0 c3 c3 66 3c 18 18 3c 66 c3 c3 6*0 c3 c3 c3 66 3c 4*18 3c 6*0 7f 63 43 6 c 18 30 61 63 7f
  //   6*0 3c 8*30 3c 6*0 80 c0 e0 70 38 1c e 7 3 1 6*0 3c 8*c 3c 4*0 8 1c 36 63 24*0 ff 0 0 0 18 18 c 18*0
  //   3c 46 6 3e 66 66 3b 6*0 70 30 30 3c 36 4*33 6e 9*0 3e 63 60 60 60 63 3e 6*0 e 6 6 1e 36 4*66 3b 9*0
  //   3e 63 63 7e 60 63 3e 6*0 1c 36 32 30 7c 4*30 78 9*0 3b 4*66 3e 6 66 3c 4*0 70 30 30 36 3b 4*33 73
  //   6*0 c c 0 1c 5*c 1e 6*0 6 6 0 e 5*6 66 66 3c 4*0 70 30 30 33 33 36 3c 36 33 73 6*0 1c 8*c 1e 9*0 6e
  //   7f 5*6b 9*0 6e 6*33 9*0 3e 5*63 3e 9*0 6e 4*33 3e 30 30 78 7*0 3b 4*66 3e 6 6 f 7*0 6e 3b 33 30 30
  //   30 78 9*0 3e 63 38 e 3 63 3e 6*0 8 18 18 7e 4*18 1b e 9*0 6*66 3b 9*0 63 63 36 36 1c 1c 8 9*0 63 63
  //   63 6b 6b 7f 36 9*0 63 36 1c 1c 1c 36 63 9*0 5*63 3f 3 6 3c 7*0 7f 66 c 18 30 63 7f 6*0 e 18 18 18 70
  //   4*18 e 6*0 5*18 0 5*18 5*0 70 18 18 18 e 4*18 70 6*0 3b 6e 13*0 70 d8 d8 70
  //   contents of rom_5 (hex, n*v repeats v):
  //   18*0 18 3c 3c 3c 18 18 18 0 18 18 5*0 63 63 63 22 14*0 36 36 7f 36 36 36 7f 36 36 4*0 c c 3e 63 61
  //   60 3e 3 3 43 63 3e c c 7*0 61 63 6 c 18 33 63 7*0 1c 36 36 1c 3b 6e 66 66 3b 5*0 30 30 30 60 13*0 c
  //   18 18 4*30 18 18 c 6*0 18 c c 4*6 c c 18 8*0 42 66 3c ff 3c 66 42 9*0 18 18 18 ff 18 18 18 15*0 18
  //   18 18 30 9*0 ff 18*0 18 18 6*0 1 3 7 e 1c 38 70 e0 c0 80 6*0 3e 63 63 63 6b 6b 63 63 63 3e 6*0 c 1c
  //   3c 6*c 3f 6*0 3e 63 3 6 c 18 30 61 63 7f 6*0 3e 63 3 3 1e 3 3 3 63 3e 6*0 6 e 1e 36 66 66 7f 6 6 f
  //   6*0 7f 60 60 60 7e 3 3 63 73 3e 6*0 1c 30 60 60 7e 4*63 3e 6*0 7f 63 3 6 6 c c 18 18 18 6*0 3e 63 63
  //   63 3e 4*63 3e 6*0 3e 4*63 3f 3 3 6 3c 9*0 18 18 0 0 0 18 18 9*0 18 18 0 0 0 18 18 18 30 5*0 6 c 18
  //   30 60 30 18 c 6 10*0 7e 0 0 7e 9*0 60 30 18 c 6 c 18 30 60 6*0 3e 63 63 6 c c c 0 c c 6*0 3e 63 63
  //   6f 6b 6b 6e 60 60 3e 6*0 8 1c 36 63 63 63 7f 63 63 63 6*0 7e 33 33 33 3e 4*33 7e 6*0 1e 33 61 4*60
  //   61 33 1e 6*0 7c 36 6*33 36 7c 6*0 7f 33 31 34 3c 34 30 31 33 7f 6*0 7f 33 31 34 3c 34 30 30 30 78
  //   6*0 1e 33 61 60 60 6f 63 63 37 1d 6*0 4*63 7f 5*63 6*0 3c 8*18 3c 6*0 f 6*6 66 66 3c 6*0 73 33 36 36
  //   3c 36 36 33 33 73 6*0 78 6*30 31 33 7f 6*0 63 77 7f 6b 6*63 6*0 63 63 73 7b 7f 6f 67 63 63 63 6*0 1c
  //   36 6*63 36 1c 6*0 7e 33 33 33 3e 4*30 78 6*0 3e 6*63 6b 6f 3e 6 7 4*0 7e 33 33 33 3e 36 36 33 33 73
  //   6*0 3e 63 63 30 1c 6 3 63 63 3e 6*0 ff db 99 6*18 3c 6*0 9*63 3e 6*0 7*63 36 1c 8 6*0 5*63 6b 6b 7f
  //   36 36 6*0 c3 c3 66 3c 18 18 3c 66 c3 c3 6*0 c3 c3 c3 66 3c 4*18 3c 6*0 7f 63 43 6 c 18 30 61 63 7f
  //   6*0 3c 8*30 3c 6*0 80 c0 e0 70 38 1c e 7 3 1 6*0 3c 8*c 3c 4*0 8 1c 36 63 24*0 ff 0 0 0 18 18 c 18*0
  //   3c 46 6 3e 66 66 3b 6*0 70 30 30 3c 36 4*33 6e 9*0 3e 63 60 60 60 63 3e 6*0 e 6 6 1e 36 4*66 3b 9*0
  //   3e 63 63 7e 60 63 3e 6*0 1c 36 32 30 7c 4*30 78 9*0 3b 4*66 3e 6 66 3c 4*0 70 30 30 36 3b 4*33 73
  //   6*0 c c 0 1c 5*c 1e 6*0 6 6 0 e 5*6 66 66 3c 4*0 70 30 30 33 33 36 3c 36 33 73 6*0 1c 8*c 1e 9*0 6e
  //   7f 5*6b 9*0 6e 6*33 9*0 3e 5*63 3e 9*0 6e 4*33 3e 30 30 78 7*0 3b 4*66 3e 6 6 f 7*0 6e 3b 33 30 30
  //   30 78 9*0 3e 63 38 e 3 63 3e 6*0 8 18 18 7e 4*18 1b e 9*0 6*66 3b 9*0 63 63 36 36 1c 1c 8 9*0 63 63
  //   63 6b 6b 7f 36 9*0 63 36 1c 1c 1c 36 63 9*0 5*63 3f 3 6 3c 7*0 7f 66 c 18 30 63 7f 6*0 e 18 18 18 70
  //   4*18 e 6*0 5*18 0 5*18 5*0 70 18 18 18 e 4*18 70 6*0 3b 6e 13*0 70 d8 d8 70
  //   contents of rom_6 (hex, n*v repeats v):
  //   18*0 18 3c 3c 3c 18 18 18 0 18 18 5*0 63 63 63 22 14*0 36 36 7f 36 36 36 7f 36 36 4*0 c c 3e 63 61
  //   60 3e 3 3 43 63 3e c c 7*0 61 63 6 c 18 33 63 7*0 1c 36 36 1c 3b 6e 66 66 3b 5*0 30 30 30 60 13*0 c
  //   18 18 4*30 18 18 c 6*0 18 c c 4*6 c c 18 8*0 42 66 3c ff 3c 66 42 9*0 18 18 18 ff 18 18 18 15*0 18
  //   18 18 30 9*0 ff 18*0 18 18 6*0 1 3 7 e 1c 38 70 e0 c0 80 6*0 3e 63 63 63 6b 6b 63 63 63 3e 6*0 c 1c
  //   3c 6*c 3f 6*0 3e 63 3 6 c 18 30 61 63 7f 6*0 3e 63 3 3 1e 3 3 3 63 3e 6*0 6 e 1e 36 66 66 7f 6 6 f
  //   6*0 7f 60 60 60 7e 3 3 63 73 3e 6*0 1c 30 60 60 7e 4*63 3e 6*0 7f 63 3 6 6 c c 18 18 18 6*0 3e 63 63
  //   63 3e 4*63 3e 6*0 3e 4*63 3f 3 3 6 3c 9*0 18 18 0 0 0 18 18 9*0 18 18 0 0 0 18 18 18 30 5*0 6 c 18
  //   30 60 30 18 c 6 10*0 7e 0 0 7e 9*0 60 30 18 c 6 c 18 30 60 6*0 3e 63 63 6 c c c 0 c c 6*0 3e 63 63
  //   6f 6b 6b 6e 60 60 3e 6*0 8 1c 36 63 63 63 7f 63 63 63 6*0 7e 33 33 33 3e 4*33 7e 6*0 1e 33 61 4*60
  //   61 33 1e 6*0 7c 36 6*33 36 7c 6*0 7f 33 31 34 3c 34 30 31 33 7f 6*0 7f 33 31 34 3c 34 30 30 30 78
  //   6*0 1e 33 61 60 60 6f 63 63 37 1d 6*0 4*63 7f 5*63 6*0 3c 8*18 3c 6*0 f 6*6 66 66 3c 6*0 73 33 36 36
  //   3c 36 36 33 33 73 6*0 78 6*30 31 33 7f 6*0 63 77 7f 6b 6*63 6*0 63 63 73 7b 7f 6f 67 63 63 63 6*0 1c
  //   36 6*63 36 1c 6*0 7e 33 33 33 3e 4*30 78 6*0 3e 6*63 6b 6f 3e 6 7 4*0 7e 33 33 33 3e 36 36 33 33 73
  //   6*0 3e 63 63 30 1c 6 3 63 63 3e 6*0 ff db 99 6*18 3c 6*0 9*63 3e 6*0 7*63 36 1c 8 6*0 5*63 6b 6b 7f
  //   36 36 6*0 c3 c3 66 3c 18 18 3c 66 c3 c3 6*0 c3 c3 c3 66 3c 4*18 3c 6*0 7f 63 43 6 c 18 30 61 63 7f
  //   6*0 3c 8*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
  //   contents of rom_7 (hex, n*v repeats v):
  //   18*0 18 3c 3c 3c 18 18 18 0 18 18 5*0 63 63 63 22 14*0 36 36 7f 36 36 36 7f 36 36 4*0 c c 3e 63 61
  //   60 3e 3 3 43 63 3e c c 7*0 61 63 6 c 18 33 63 7*0 1c 36 36 1c 3b 6e 66 66 3b 5*0 30 30 30 60 13*0 c
  //   18 18 4*30 18 18 c 6*0 18 c c 4*6 c c 18 8*0 42 66 3c ff 3c 66 42 9*0 18 18 18 ff 18 18 18 15*0 18
  //   18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
  //   contents of rom_8 (hex, n*v repeats v):
  //   18*0 18 3c 3c 3c 18 18 18 0 18 18 5*0 63 63 63 22 14*0 36 36 7f 36 36 36 7f 36 36 4*0 c c 3e 63 61
  //   60 3e 3 3 43 63 3e c c 7*0 61 63 6 c 18 33 63 7*0 1c 36 36 1c 3b 6e 66 66 3b 5*0 30 30 30 60 13*0 c
  //   18 18 4*30 18 18 c 6*0 18 c c 4*6 c c 18 8*0 42 66 3c ff 3c 66 42 9*0 18 18 18 ff 18 18 18 15*0 18
  //   18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
  //   contents of rom_9 (hex, n*v repeats v):
  //   18*0 18 3c 3c 3c 18 18 18 0 18 18 5*0 63 63 63 22 14*0 36 36 7f 36 36 36 7f 36 36 4*0 c c 3e 63 61
  //   60 3e 3 3 43 63 3e c c 7*0 61 63 6 c 18 33 63 7*0 1c 36 36 1c 3b 6e 66 66 3b 5*0 30 30 30 60 13*0 c
  //   18 18 4*30 18 18 c 6*0 18 c c 4*6 c c 18 8*0 42 66 3c ff 3c 66 42 9*0 18 18 18 ff 18 18 18 15*0 18
  //   18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
  //   contents of rom_10 (hex, n*v repeats v):
  //   18*0 18 3c 3c 3c 18 18 18 0 18 18 5*0 63 63 63 22 14*0 36 36 7f 36 36 36 7f 36 36 4*0 c c 3e 63 61
  //   60 3e 3 3 43 63 3e c c 7*0 61 63 6 c 18 33 63 7*0 1c 36 36 1c 3b 6e 66 66 3b 5*0 30 30 30 60 13*0 c
  //   18 18 4*30 18 18 c 6*0 18 c c 4*6 c c 18 8*0 42 66 3c ff 3c 66 42 9*0 18 18 18 ff 18 18 18 15*0 18
  //   18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
  //   contents of rom_11 (hex, n*v repeats v):
  //   18*0 18 3c 3c 3c 18 18 18 0 18 18 5*0 63 63 63 22 14*0 36 36 7f 36 36 36 7f 36 36 4*0 c c 3e 63 61
  //   60 3e 3 3 43 63 3e c c 7*0 61 63 6 c 18 33 63 7*0 1c 36 36 1c 3b 6e 66 66 3b 5*0 30 30 30 60 13*0 c
  //   18 18 4*30 18 18 c 6*0 18 c c 4*6 c c 18 8*0 42 66 3c ff 3c 66 42 9*0 18 18 18 ff 18 18 18 15*0 18
  //   18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
  //   contents of rom_12 (hex, n*v repeats v):
  //   18*0 18 3c 3c 3c 18 18 18 0 18 18 5*0 63 63 63 22 14*0 36 36 7f 36 36 36 7f 36 36 4*0 c c 3e 63 61
  //   60 3e 3 3 43 63 3e c c 7*0 61 63 6 c 18 33 63 7*0 1c 36 36 1c 3b 6e 66 66 3b 5*0 30 30 30 60 13*0 c
  //   18 18 4*30 18 18 c 6*0 18 c c 4*6 c c 18 8*0 42 66 3c ff 3c 66 42 9*0 18 18 18 ff 18 18 18 15*0 18
  //   18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
  //   contents of rom_13 (hex, n*v repeats v):
  //   18*0 18 3c 3c 3c 18 18 18 0 18 18 5*0 63 63 63 22 14*0 36 36 7f 36 36 36 7f 36 36 4*0 c c 3e 63 61
  //   60 3e 3 3 43 63 3e c c 7*0 61 63 6 c 18 33 63 7*0 1c 36 36 1c 3b 6e 66 66 3b 5*0 30 30 30 60 13*0 c
  //   18 18 4*30 18 18 c 6*0 18 c c 4*6 c c 18 8*0 42 66 3c ff 3c 66 42 9*0 18 18 18 ff 18 18 18 15*0 18
  //   18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
  //   contents of rom_14 (hex, n*v repeats v):
  //   18*0 18 3c 3c 3c 18 18 18 0 18 18 5*0 63 63 63 22 14*0 36 36 7f 36 36 36 7f 36 36 4*0 c c 3e 63 61
  //   60 3e 3 3 43 63 3e c c 7*0 61 63 6 c 18 33 63 7*0 1c 36 36 1c 3b 6e 66 66 3b 5*0 30 30 30 60 13*0 c
  //   18 18 4*30 18 18 c 6*0 18 c c 4*6 c c 18 8*0 42 66 3c ff 3c 66 42 9*0 18 18 18 ff 18 18 18 15*0 18
  //   18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
  //   contents of rom_15 (hex, n*v repeats v):
  //   18*0 18 3c 3c 3c 18 18 18 0 18 18 5*0 63 63 63 22 14*0 36 36 7f 36 36 36 7f 36 36 4*0 c c 3e 63 61
  //   60 3e 3 3 43 63 3e c c 7*0 61 63 6 c 18 33 63 7*0 1c 36 36 1c 3b 6e 66 66 3b 5*0 30 30 30 60 13*0 c
  //   18 18 4*30 18 18 c 6*0 18 c c 4*6 c c 18 8*0 42 66 3c ff 3c 66 42 9*0 18 18 18 ff 18 18 18 15*0 18
  //   18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
  //   contents of rom_16 (hex, n*v repeats v):
  //   18*0 18 3c 3c 3c 18 18 18 0 18 18 5*0 63 63 63 22 14*0 36 36 7f 36 36 36 7f 36 36 4*0 c c 3e 63 61
  //   60 3e 3 3 43 63 3e c c 7*0 61 63 6 c 18 33 63 7*0 1c 36 36 1c 3b 6e 66 66 3b 5*0 30 30 30 60 13*0 c
  //   18 18 4*30 18 18 c 6*0 18 c c 4*6 c c 18 8*0 42 66 3c ff 3c 66 42 9*0 18 18 18 ff 18 18 18 15*0 18
  //   18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
endmodule

module \灯  (
  input  in_1
);

  wire clock_1_out;
  wire [7:0] adder_1_out, adder_2_out, \ascii码显示实验_1_out_3 , \ascii码显示实验_1_out_4 , \ascii码显示实验_1_out_5 ,
       \ascii码显示实验_1_out_6 , \ascii码显示实验_1_out_7 , \ascii码显示实验_1_out_8 , \ascii码显示实验_1_out_9 ,
       \ascii码显示实验_1_out_10 , \ascii码显示实验_1_out_11 , \ascii码显示实验_1_out_12 , \ascii码显示实验_1_out_13 ,
       \ascii码显示实验_1_out_14 , \ascii码显示实验_1_out_15 , \ascii码显示实验_1_out_16 , \ascii码显示实验_1_out_17 ,
       \ascii码显示实验_1_out_18 , \ascii码显示实验_2_out_3 , \ascii码显示实验_2_out_4 , \ascii码显示实验_2_out_5 ,
       \ascii码显示实验_2_out_6 , \ascii码显示实验_2_out_7 , \ascii码显示实验_2_out_8 , \ascii码显示实验_2_out_9 ,
       \ascii码显示实验_2_out_10 , \ascii码显示实验_2_out_11 , \ascii码显示实验_2_out_12 , \ascii码显示实验_2_out_13 ,
       \ascii码显示实验_2_out_14 , \ascii码显示实验_2_out_15 , \ascii码显示实验_2_out_16 , \ascii码显示实验_2_out_17 ,
       \ascii码显示实验_2_out_18 , \ascii码显示实验_3_out_3 , \ascii码显示实验_3_out_4 , \ascii码显示实验_3_out_5 ,
       \ascii码显示实验_3_out_6 , \ascii码显示实验_3_out_7 , \ascii码显示实验_3_out_8 , \ascii码显示实验_3_out_9 ,
       \ascii码显示实验_3_out_10 , \ascii码显示实验_3_out_11 , \ascii码显示实验_3_out_12 , \ascii码显示实验_3_out_13 ,
       \ascii码显示实验_3_out_14 , \ascii码显示实验_3_out_15 , \ascii码显示实验_3_out_16 , \ascii码显示实验_3_out_17 ,
       \ascii码显示实验_3_out_18 , counter_1_q;

  Clock clock_1 (.out(clock_1_out));
  Counter #(.max('h50)) counter_1 (
    .Q(counter_1_q), .clk(clock_1_out));  // open: load, D, count, carry, clr, preset, down
  Adder adder_1 (.a(counter_1_q), .b(8'h10), .out(adder_1_out));  // open: cin, cout
  Adder adder_2 (.a(adder_1_out), .b(8'h10), .out(adder_2_out));  // open: cin, cout
  \ASCII码显示实验  \ascii码显示实验_1  (
    .ASCII_CODE(counter_1_q), .Sel(in_1), .out_3(\ascii码显示实验_1_out_3 ), .out_4(\ascii码显示实验_1_out_4 ),
    .out_5(\ascii码显示实验_1_out_5 ), .out_6(\ascii码显示实验_1_out_6 ), .out_7(\ascii码显示实验_1_out_7 ),
    .out_8(\ascii码显示实验_1_out_8 ), .out_9(\ascii码显示实验_1_out_9 ), .out_10(\ascii码显示实验_1_out_10 ),
    .out_11(\ascii码显示实验_1_out_11 ), .out_12(\ascii码显示实验_1_out_12 ), .out_13(\ascii码显示实验_1_out_13 ),
    .out_14(\ascii码显示实验_1_out_14 ), .out_15(\ascii码显示实验_1_out_15 ), .out_16(\ascii码显示实验_1_out_16 ),
    .out_17(\ascii码显示实验_1_out_17 ), .out_18(\ascii码显示实验_1_out_18 ));
  DotMatrix #(.inputtype("row"), .matrixcols(8), .matrixrows(16)) dotmatrix_1 (
    .row0(\ascii码显示实验_1_out_3 ), .row1(\ascii码显示实验_1_out_4 ), .row2(\ascii码显示实验_1_out_5 ),
    .row3(\ascii码显示实验_1_out_6 ), .row4(\ascii码显示实验_1_out_7 ), .row5(\ascii码显示实验_1_out_8 ),
    .row6(\ascii码显示实验_1_out_9 ), .row7(\ascii码显示实验_1_out_10 ), .row8(\ascii码显示实验_1_out_11 ),
    .row9(\ascii码显示实验_1_out_12 ), .row10(\ascii码显示实验_1_out_13 ), .row11(\ascii码显示实验_1_out_14 ),
    .row12(\ascii码显示实验_1_out_15 ), .row13(\ascii码显示实验_1_out_16 ), .row14(\ascii码显示实验_1_out_17 ),
    .row15(\ascii码显示实验_1_out_18 ));
  DotMatrix #(.inputtype("row"), .matrixcols(8), .matrixrows(16)) dotmatrix_2 (
    .row0(\ascii码显示实验_2_out_3 ), .row1(\ascii码显示实验_2_out_4 ), .row2(\ascii码显示实验_2_out_5 ),
    .row3(\ascii码显示实验_2_out_6 ), .row4(\ascii码显示实验_2_out_7 ), .row5(\ascii码显示实验_2_out_8 ),
    .row6(\ascii码显示实验_2_out_9 ), .row7(\ascii码显示实验_2_out_10 ), .row8(\ascii码显示实验_2_out_11 ),
    .row9(\ascii码显示实验_2_out_12 ), .row10(\ascii码显示实验_2_out_13 ), .row11(\ascii码显示实验_2_out_14 ),
    .row12(\ascii码显示实验_2_out_15 ), .row13(\ascii码显示实验_2_out_16 ), .row14(\ascii码显示实验_2_out_17 ),
    .row15(\ascii码显示实验_2_out_18 ));
  \ASCII码显示实验  \ascii码显示实验_2  (
    .ASCII_CODE(adder_1_out), .Sel(in_1), .out_3(\ascii码显示实验_2_out_3 ), .out_4(\ascii码显示实验_2_out_4 ),
    .out_5(\ascii码显示实验_2_out_5 ), .out_6(\ascii码显示实验_2_out_6 ), .out_7(\ascii码显示实验_2_out_7 ),
    .out_8(\ascii码显示实验_2_out_8 ), .out_9(\ascii码显示实验_2_out_9 ), .out_10(\ascii码显示实验_2_out_10 ),
    .out_11(\ascii码显示实验_2_out_11 ), .out_12(\ascii码显示实验_2_out_12 ), .out_13(\ascii码显示实验_2_out_13 ),
    .out_14(\ascii码显示实验_2_out_14 ), .out_15(\ascii码显示实验_2_out_15 ), .out_16(\ascii码显示实验_2_out_16 ),
    .out_17(\ascii码显示实验_2_out_17 ), .out_18(\ascii码显示实验_2_out_18 ));
  \ASCII码显示实验  \ascii码显示实验_3  (
    .ASCII_CODE(adder_2_out), .Sel(in_1), .out_3(\ascii码显示实验_3_out_3 ), .out_4(\ascii码显示实验_3_out_4 ),
    .out_5(\ascii码显示实验_3_out_5 ), .out_6(\ascii码显示实验_3_out_6 ), .out_7(\ascii码显示实验_3_out_7 ),
    .out_8(\ascii码显示实验_3_out_8 ), .out_9(\ascii码显示实验_3_out_9 ), .out_10(\ascii码显示实验_3_out_10 ),
    .out_11(\ascii码显示实验_3_out_11 ), .out_12(\ascii码显示实验_3_out_12 ), .out_13(\ascii码显示实验_3_out_13 ),
    .out_14(\ascii码显示实验_3_out_14 ), .out_15(\ascii码显示实验_3_out_15 ), .out_16(\ascii码显示实验_3_out_16 ),
    .out_17(\ascii码显示实验_3_out_17 ), .out_18(\ascii码显示实验_3_out_18 ));
  DotMatrix #(.inputtype("row"), .matrixcols(8), .matrixrows(16)) dotmatrix_3 (
    .row0(\ascii码显示实验_3_out_3 ), .row1(\ascii码显示实验_3_out_4 ), .row2(\ascii码显示实验_3_out_5 ),
    .row3(\ascii码显示实验_3_out_6 ), .row4(\ascii码显示实验_3_out_7 ), .row5(\ascii码显示实验_3_out_8 ),
    .row6(\ascii码显示实验_3_out_9 ), .row7(\ascii码显示实验_3_out_10 ), .row8(\ascii码显示实验_3_out_11 ),
    .row9(\ascii码显示实验_3_out_12 ), .row10(\ascii码显示实验_3_out_13 ), .row11(\ascii码显示实验_3_out_14 ),
    .row12(\ascii码显示实验_3_out_15 ), .row13(\ascii码显示实验_3_out_16 ), .row14(\ascii码显示实验_3_out_17 ),
    .row15(\ascii码显示实验_3_out_18 ));
endmodule
