// Logisim project lab6.circ as structural Verilog: 6 circuits, main circuit 单周期CPU
module \单周期CPU  (
  input  [31:0] Initial_Address,
  output halt
);

  wire alu_1_p5, branch_1_nxtasrc, branch_1_nxtbsrc, clk, clock_2_out, Halt0, not_1_out, or_1_out, RESET,
       \控制器_1_aluasrc , \控制器_1_memtoreg , \控制器_1_memwr , \控制器_1_regwr ;
  wire [1:0] \控制器_1_alubsrc ;
  wire [2:0] idu_1_funct3, \控制器_1_branch , \控制器_1_extop , \控制器_1_memop ;
  wire [3:0] \控制器_1_aluctr ;
  wire [6:0] idu_1_funct7, idu_1_opcode;
  wire [15:0] counter_1_q;
  wire [31:0] alu_1_p4, idu_1_busa, idu_1_busb, idu_1_dataa, idu_1_datab, idu_1_imm, ifu_1_pc, IR,
       multiplexer_1_out, \数据存储器_1_dataout ;

  IFU ifu_1 (
    .PC(ifu_1_pc), .Initial_Address(Initial_Address), .BusA(idu_1_busa), .Halt(halt),
    .NxtASrc(branch_1_nxtasrc), .NxtBSrc(branch_1_nxtbsrc), .Imm(idu_1_imm), .CLK(clk), .Reset(RESET));  // open: IR
  Clock clock_1 (.out(clk));
  Button u_Reset (.out(RESET));
  ROM #(.addrWidth(16), .dataWidth(32), .Select("high")) \u_指令存储器  (.addr(ifu_1_pc[17:2]), .data(IR));
  \控制器  \u_控制器_1  (
    .funct3(idu_1_funct3), .opcode(idu_1_opcode), .Branch(\控制器_1_branch ), .MemOp(\控制器_1_memop ),
    .ALUASrc(\控制器_1_aluasrc ), .ALUBSrc(\控制器_1_alubsrc ), .ALUctr(\控制器_1_aluctr ),
    .MemtoReg(\控制器_1_memtoreg ), .RegWr(\控制器_1_regwr ), .MemWr(\控制器_1_memwr ), .ExtOp(\控制器_1_extop ),
    .funct7(idu_1_funct7), .halt(halt));
  lab5_IDU idu_1 (
    .ExtOp(\控制器_1_extop ), .RegWr(\控制器_1_regwr ), .OpCode(idu_1_opcode), .ALUASrc(\控制器_1_aluasrc ),
    .ALUBSrc(\控制器_1_alubsrc ), .Funct3(idu_1_funct3), .Funct7(idu_1_funct7), .IR(IR),
    .BusW(multiplexer_1_out), .PC(ifu_1_pc), .DataA(idu_1_dataa), .BusB(idu_1_busb), .DataB(idu_1_datab),
    .Imm(idu_1_imm), .BusA(idu_1_busa), .in_8(clk));
  // ALU alu_1: pin names not known; wires that end beside it: idu_1_dataa, idu_1_datab, \控制器_1_aluctr , alu_1_p4, alu_1_p5
  or or_1 (or_1_out, halt, Halt0);
  Branch branch_1 (
    .Branch(\控制器_1_branch ), .NxtASrc(branch_1_nxtasrc), .Zero(alu_1_p5), .NxtBSrc(branch_1_nxtbsrc),
    .Result0(alu_1_p4[0]));
  Comparator #(.width(32)) comparator_1 (.a(IR), .b(32'h6f), .eq(Halt0));  // open: gt, lt
  Counter #(.width(16), .max('hffff), .behavior("old")) counter_1 (
    .count(not_1_out), .Q(counter_1_q), .clk(clock_2_out), .clr(RESET));  // open: load, D, carry, preset
  // Probe on counter_1_q
  not not_1 (not_1_out, or_1_out);
  Clock clock_2 (.out(clock_2_out));
  \数据存储器  \u_数据存储器_1  (
    .Addr(alu_1_p4[17:2]), .Din(idu_1_busb), .DataOut(\数据存储器_1_dataout ), .CLK(clk), .CLR(RESET),
    .MemOp(\控制器_1_memop ), .WE(\控制器_1_memwr ), .SEL(1'b1));
  Multiplexer #(.width(32), .enable("false")) multiplexer_1 (
    .in0(alu_1_p4), .in1(\数据存储器_1_dataout ), .out(multiplexer_1_out), .sel(\控制器_1_memtoreg ));

  // Other names for the same wires on the sheet: Init_Addr[31:0] = Initial_Address

  // Notes on the sheet:
  //   取指令部件
  //   输入信号
  //   RV32I单周期CPU设计
  //   输出信号
  //   数据通路
  //   ALU
  //   数据存储器
  //   程序执行周期数
endmodule

module \控制器  (
  input  [6:0] opcode,
  input  [2:0] funct3,
  input  [6:0] funct7,
  output [2:0] ExtOp,
  output RegWr,
  output ALUASrc,
  output [1:0] ALUBSrc,
  output [3:0] ALUctr,
  output [2:0] Branch,
  output MemtoReg,
  output [2:0] MemOp,
  output MemWr,
  output halt
);

  wire and_1_out, and_2_out, and_3_out, and_4_out, and_5_out, and_6_out, and_7_out, and_8_out, and_9_out,
       and_10_out, and_11_out, and_12_out, I_Arith, J_jal, J_jalr, or_1_out, or_2_out, or_4_out, or_5_out,
       or_13_out, or_15_out, or_17_out, R_Arith, U_auipc, U_lui;

  Extop extop_1 (.in_1(opcode[6]), .in_2(opcode[5]), .in_3(opcode[3]), .in_4(opcode[2]), .out_5(ExtOp));
  and and_1 (and_1_out, funct3[0], I_Arith);
  and and_2 (and_2_out, I_Arith, funct3[2]);
  and and_3 (and_3_out, funct3[2], R_Arith);
  and and_4 (and_4_out, funct3[0], R_Arith);
  and and_5 (and_5_out, I_Arith, funct3[1]);
  Comparator #(.width(7)) comparator_1 (.a(opcode), .b(7'b0110111), .eq(U_lui));  // open: gt, lt
  Comparator #(.width(7)) comparator_2 (.a(opcode), .b(7'b1100111), .eq(J_jalr));  // open: gt, lt
  and and_6 (and_6_out, funct3[0], Branch[2]);
  and and_7 (and_7_out, funct3[1], Branch[2]);
  and and_8 (and_8_out, R_Arith, funct3[1]);
  or or_1 (or_1_out, MemWr, MemtoReg);
  and and_9 (and_9_out, funct3[2], Branch[2]);
  Comparator #(.width(7)) comparator_3 (.a(opcode), .b(7'b0010111), .eq(U_auipc));  // open: gt, lt
  Comparator #(.width(7)) comparator_4 (.a(opcode), .b(7'b1100011), .eq(Branch[2]));  // open: gt, lt
  or or_2 (or_2_out, U_lui, U_auipc);
  or or_3 (ALUBSrc[0], J_jal, J_jalr);
  MemOp memop_1 (
    ._2(funct3[2]), ._1(funct3[1]), ._0(funct3[0]), ._2_2(MemOp[2]), ._1_2(MemOp[1]), ._0_2(MemOp[0]),
    .s(or_1_out));
  and and_10 (and_10_out, I_Arith, and_11_out);
  and and_11 (and_11_out, funct3[0], ~funct3[1], funct3[2]);  // AND_Gate
  or or_4 (or_4_out, and_10_out, funct7[5]);
  and and_12 (and_12_out, funct7[5], R_Arith);
  Comparator #(.width(7)) comparator_5 (.a(opcode), .b(7'b0010011), .eq(I_Arith));  // open: gt, lt
  Comparator #(.width(7)) comparator_6 (.a(opcode), .b(7'b0000011), .eq(MemtoReg));  // open: gt, lt
  or or_5 (or_5_out, or_4_out, and_12_out);
  Comparator #(.width(7)) comparator_7 (.a(opcode), .b(7'b0110011), .eq(R_Arith));  // open: gt, lt
  Comparator #(.width(7)) comparator_8 (.a(opcode), .b(7'b0100011), .eq(MemWr));  // open: gt, lt
  or or_6 (RegWr, or_2_out, ALUBSrc[0], I_Arith, R_Arith, MemtoReg);
  or or_7 (ALUASrc, U_auipc, ALUBSrc[0]);
  or or_8 (ALUBSrc[1], or_2_out, I_Arith, MemtoReg, MemWr);
  or or_9 (Branch[1], and_9_out, J_jalr);
  or or_10 (Branch[0], J_jal, and_6_out);
  Comparator #(.width(7)) comparator_9 (.a(opcode), .b(7'b1101111), .eq(J_jal));  // open: gt, lt
  Comparator #(.width(7)) comparator_10 (.a(opcode), .b({7{1'b0}}), .eq(halt));  // open: gt, lt
  or or_11 (ALUctr[3], U_lui, or_5_out);
  or or_12 (ALUctr[2], U_lui, or_13_out);
  or or_13 (or_13_out, and_2_out, and_3_out);
  or or_14 (ALUctr[1], U_lui, or_15_out);
  or or_15 (or_15_out, and_5_out, and_8_out, Branch[2]);
  or or_16 (ALUctr[0], U_lui, or_17_out);
  or or_17 (or_17_out, and_4_out, and_1_out, and_7_out);

  // Other names for the same wires on the sheet: B_Instr = Branch[2]; I_load = MemtoReg; S_Instr = MemWr

  // Notes on the sheet:
  //   输入信号
  //   提示：根据指令种类和代码，把7位指令code用一位标志位来表示。
  //   输出信号
endmodule

module main (
  input  a,
  input  b,
  input  c,
  output x,
  output x2,
  output x3
);

  wire not_1_out, not_2_out, not_3_out, not_4_out;

  not not_1 (not_1_out, a);
  not not_2 (not_2_out, b);
  not not_3 (not_3_out, b);
  not not_4 (not_4_out, c);
  and and_1 (x, not_1_out, not_2_out);
  and and_2 (x3, not_3_out, not_4_out);

  assign x2 = c;
endmodule

module Extop (
  input  in_1,
  input  in_2,
  input  in_3,
  input  in_4,
  output [2:0] out_5
);

  wire and_2_out, and_3_out, not_1_out, not_2_out, not_3_out;

  not not_1 (not_1_out, in_4);
  not not_2 (not_2_out, in_1);
  not not_3 (not_3_out, in_4);
  and and_1 (out_5[1], in_2, not_1_out);
  and and_2 (and_2_out, not_2_out, in_4);
  and and_3 (and_3_out, in_1, not_3_out);
  or or_1 (out_5[0], and_2_out, and_3_out);

  assign out_5[2] = in_3;
endmodule

module MemOp (
  input  _2,
  input  _1,
  input  _0,
  input  s,
  output _2_2,
  output _1_2,
  output _0_2
);

  wire and_1_out, and_2_out, not_1_out, not_2_out, not_3_out, not_4_out;

  not not_1 (not_1_out, _2);
  not not_2 (not_2_out, _1);
  not not_3 (not_3_out, _1);
  not not_4 (not_4_out, _0);
  and and_1 (and_1_out, not_1_out, not_2_out);
  and and_2 (and_2_out, not_3_out, not_4_out);
  and and_3 (_2_2, and_1_out, s);
  and and_4 (_1_2, _0, s);
  and and_5 (_0_2, and_2_out, s);
endmodule

module IDU (
  input  [31:0] IR,
  input  [31:0] BusW,
  input  [31:0] PC,
  input  [2:0] ExtOp,
  input  RegWr,
  input  ALUASrc,
  input  [1:0] ALUBSrc,
  input  in_8,
  output [31:0] DataA,
  output [31:0] DataB,
  output [31:0] BusA,
  output [6:0] OpCode,
  output [31:0] BusB,
  output [31:0] Imm,
  output [2:0] Funct3,
  output [6:0] Funct7
);

  \立即数扩展器  \u_立即数扩展器_1  (.Instr(IR), .Extop(ExtOp), .imm(Imm));
  RegFile regfile_1 (
    .R1_num(IR[19:15]), .R2_num(IR[24:20]), .Din(BusW), .Reg1Out(BusA), .Reg2Out(BusB),
    .Write_Reg_num(IR[11:7]), .Write_Enable(RegWr), .Clock(in_8));
  Multiplexer #(.width(32), .enable("false")) multiplexer_1 (.in0(BusA), .in1(PC), .out(DataA), .sel(ALUASrc));
  Multiplexer #(.select(2), .width(32), .enable("false")) multiplexer_2 (
    .in0(BusB), .in1(32'h4), .in2(Imm), .out(DataB), .sel(ALUBSrc));  // open: in3

  assign Funct3 = IR[14:12];
  assign Funct7 = IR[31:25];
  assign OpCode = IR[6:0];

  // Other names for the same wires on the sheet: clk = in_8; DataIn[31:0] = BusB; op[6:0] = IR[6:0]

  // Notes on the sheet:
  //   PC: pull=down
  //   BusW: pull=down
  //   RegWr: pull=down
  //   ALUASrc: pull=down
  //   ALUBSrc: pull=down
  //   ExtOp: pull=down
  //   指令解析
  //   输入信号
  //   访问寄存器堆
  //   输出信号
  //   输出数据
endmodule
